// Logisim project 7seg_display.circ as structural Verilog: 8 circuits, main circuit main
module main (
  input  [2:0] in_1
);

  wire Output_a_out_4, Output_b_out_4, output_c_1_out_4, output_d_1_out_4, output_e_1_out_4,
       output_f_1_out_4, output_g_1_out_4;

  output_a Output_a (.in_1(in_1[2]), .in_2(in_1[1]), .in_3(in_1[0]), .out_4(Output_a_out_4));
  output_b Output_b (.in_1(in_1[2]), .in_2(in_1[1]), .in_3(in_1[0]), .out_4(Output_b_out_4));
  output_c output_c_1 (.in_1(in_1[2]), .in_2(in_1[1]), .in_3(in_1[0]), .out_4(output_c_1_out_4));
  output_d output_d_1 (.in_1(in_1[2]), .in_2(in_1[1]), .in_3(in_1[0]), .out_4(output_d_1_out_4));
  output_e output_e_1 (.in_1(in_1[2]), .in_2(in_1[1]), .in_3(in_1[0]), .out_4(output_e_1_out_4));
  output_f output_f_1 (.in_1(in_1[2]), .in_2(in_1[1]), .in_3(in_1[0]), .out_4(output_f_1_out_4));
  output_g output_g_1 (.in_1(in_1[2]), .in_2(in_1[1]), .in_3(in_1[0]), .out_4(output_g_1_out_4));
  _7_Segment_Display u_7_segment_display_1 (
    .g(Output_a_out_4), .f(Output_b_out_4), .a(output_c_1_out_4), .b(output_d_1_out_4), .e(output_e_1_out_4),
    .d(output_f_1_out_4), .c(output_g_1_out_4));  // open: dp
endmodule

module output_a (
  input  in_1,
  input  in_2,
  input  in_3,
  output out_4
);

  wire and_1_out, and_2_out, and_3_out, not_1_out, not_2_out, not_3_out, or_1_out;

  not not_1 (not_1_out, in_1);
  not not_2 (not_2_out, in_2);
  not not_3 (not_3_out, in_3);
  and and_1 (and_1_out, not_1_out, in_2);
  and and_2 (and_2_out, in_2, in_2, not_3_out);
  or or_1 (or_1_out, not_2_out, and_2_out);
  and and_3 (and_3_out, in_1, or_1_out);
  or or_2 (out_4, and_1_out, and_3_out);
endmodule

module output_b (
  input  in_1,
  input  in_2,
  input  in_3,
  output out_4
);

  wire and_1_out, and_2_out, and_3_out, not_1_out, not_2_out, not_3_out, or_1_out;

  not not_1 (not_1_out, in_1);
  not not_2 (not_2_out, in_2);
  not not_3 (not_3_out, in_3);
  and and_1 (and_1_out, in_2, not_3_out);
  or or_1 (or_1_out, not_2_out, and_1_out);
  and and_2 (and_2_out, not_1_out, not_2_out, not_3_out);
  and and_3 (and_3_out, in_1, or_1_out);
  or or_2 (out_4, and_2_out, and_3_out);
endmodule

module output_c (
  input  in_1,
  input  in_2,
  input  in_3,
  output out_4
);

  wire and_1_out, and_2_out, and_3_out, and_4_out, not_1_out, not_2_out, not_3_out, or_1_out, or_2_out;

  not not_1 (not_1_out, in_1);
  not not_2 (not_2_out, in_2);
  not not_3 (not_3_out, in_3);
  and and_1 (and_1_out, not_2_out, not_3_out);
  and and_2 (and_2_out, not_2_out, in_3);
  or or_1 (or_1_out, and_1_out, in_2);
  or or_2 (or_2_out, in_2, and_2_out);
  and and_3 (and_3_out, not_1_out, or_1_out);
  and and_4 (and_4_out, in_1, or_2_out);
  or or_3 (out_4, and_3_out, and_4_out);
endmodule

module output_d (
  input  in_1,
  input  in_2,
  input  in_3,
  output out_4
);

  wire and_1_out, and_2_out, and_3_out, not_1_out, not_2_out, not_3_out, or_1_out;

  not not_1 (not_1_out, in_1);
  not not_2 (not_2_out, in_2);
  not not_3 (not_3_out, in_3);
  and and_1 (and_1_out, in_2, in_3);
  and and_2 (and_2_out, not_2_out, not_3_out);
  and and_3 (and_3_out, in_1, or_1_out);
  or or_1 (or_1_out, and_1_out, and_2_out);
  or or_2 (out_4, not_1_out, and_3_out);
endmodule

module output_e (
  input  in_1,
  input  in_2,
  input  in_3,
  output out_4
);

  wire and_1_out, not_1_out, not_3_out, or_1_out;

  not not_1 (not_1_out, in_1);
  // NOT_Gate not_2 has open pins: in=in_2, out=open
  not not_3 (not_3_out, in_3);
  and and_1 (and_1_out, in_1, in_2);
  or or_1 (or_1_out, not_1_out, and_1_out);
  and and_2 (out_4, or_1_out, not_3_out);
endmodule

module output_f (
  input  in_1,
  input  in_2,
  input  in_3,
  output out_4
);

  wire and_1_out, and_2_out, and_3_out, and_4_out, and_5_out, not_1_out, not_2_out, not_3_out, or_1_out,
       or_2_out;

  not not_1 (not_1_out, in_1);
  not not_2 (not_2_out, in_2);
  not not_3 (not_3_out, in_3);
  and and_1 (and_1_out, in_2, in_3);
  and and_2 (and_2_out, not_2_out, in_3);
  and and_3 (and_3_out, in_2, not_3_out);
  or or_1 (or_1_out, and_1_out, not_3_out);
  or or_2 (or_2_out, and_2_out, and_3_out);
  and and_4 (and_4_out, not_1_out, or_1_out);
  and and_5 (and_5_out, in_1, or_2_out);
  or or_3 (out_4, and_4_out, and_5_out);
endmodule

module output_g (
  input  in_1,
  input  in_2,
  input  in_3,
  output out_4
);

  wire and_1_out, and_2_out, not_1_out, not_2_out, or_1_out;

  not not_1 (not_1_out, in_1);
  not not_2 (not_2_out, in_2);
  // NOT_Gate not_3 has open pins: in=in_3, out=open
  and and_1 (and_1_out, in_2, in_3);
  or or_1 (or_1_out, not_2_out, and_1_out);
  and and_2 (and_2_out, not_1_out, or_1_out);
  or or_2 (out_4, in_1, and_2_out);
endmodule
