// Logisim project vraag3.circ as structural Verilog: 2 circuits, main circuit main
module main (
  input  A,
  input  B,
  input  A_2,
  input  A_3,
  input  B_2,
  output out_6,
  output out_7,
  output out_8
);

  wire nand_1_out_3, nand_2_out_3, nand_4_out_3;

  NAND nand_1 (.A(A), .B(A), .out_3(nand_1_out_3));
  NAND nand_2 (.A(B), .B(B), .out_3(nand_2_out_3));
  NAND nand_3 (.A(A_2), .B(A_2), .out_3(out_7));
  NAND nand_4 (.A(A_3), .B(B_2), .out_3(nand_4_out_3));
  NAND nand_5 (.A(nand_4_out_3), .B(nand_4_out_3), .out_3(out_8));
  NAND nand_6 (.A(nand_1_out_3), .B(nand_2_out_3), .out_3(out_6));

  // Notes on the sheet:
  //   BUILDING OR GATE USING NAND GATE
  //   BUILDING NOT GATE USING NAND
  //   BUILDING AND GATE USING NAND GATE
endmodule

module NAND (
  input  A,
  input  B,
  output out_3
);

  wire and_1_out;

  and and_1 (and_1_out, A, B);
  not not_1 (out_3, and_1_out);
endmodule
