// Logisim project vraag4.circ as structural Verilog: 1 circuit, main circuit main
module main (
  input  A,
  input  B,
  input  C,
  output out_4,
  output out_5
);

  wire and_1_out, and_2_out, and_3_out, and_4_out, and_5_out, and_6_out, not_1_out, not_2_out, not_3_out,
       not_4_out, not_5_out, not_6_out, not_7_out, not_8_out, not_9_out, or_1_out, or_2_out, or_3_out;

  not not_1 (not_1_out, C);
  not not_2 (not_2_out, B);
  not not_3 (not_3_out, A);
  and and_1 (and_1_out, A, not_1_out);
  not not_4 (not_4_out, A);
  not not_5 (not_5_out, C);
  not not_6 (not_6_out, A);
  not not_7 (not_7_out, C);
  not not_8 (not_8_out, B);
  and and_2 (and_2_out, not_4_out, not_5_out);
  and and_3 (and_3_out, not_6_out, C);
  and and_4 (and_4_out, not_7_out, A);
  or or_1 (or_1_out, and_2_out, and_3_out);
  or or_2 (or_2_out, not_3_out, and_1_out);
  not not_9 (not_9_out, C);
  and and_5 (and_5_out, or_2_out, or_2_out, not_2_out);
  and and_6 (and_6_out, B, not_9_out, not_9_out);
  or or_3 (or_3_out, or_1_out, and_4_out);
  and and_7 (out_4, or_3_out, not_8_out);
  or or_4 (out_5, and_5_out, and_6_out);

  // Notes on the sheet:
  //   ¬A
  //   A.¬C
  //   ¬B
  //   (¬A.¬C)
  //   ¬A.C
  //   ¬C.A
  //   ¬B
  //   ¬A.¬C + ¬A.C
  //   ¬A + A.¬C
  //   ¬B(¬A + A.¬C)
  //    B.¬C
  //   (¬A .¬C + ¬A.C )+ A.¬C)
  //   X-output
  //   ¬B(¬A .¬C + ¬A.C + A.¬C)
  //   Y-output
  //   ¬B(¬A + A.¬C) + B.¬C
endmodule
