// Logisim project 12-Bit_Full_RCA.circ as structural Verilog
module _1_Bit_Adder (
  input  A,
  input  B,
  input  Cin,
  output Cout,
  output Sum
);

  wire and_1_out, and_2_out, and_3_out, and_4_out, and_5_out, and_6_out, not_1_out, not_2_out, not_3_out,
       or_1_out, or_2_out, xor_1_out;

  not not_1 (not_1_out, A);
  not not_2 (not_2_out, B);
  not not_3 (not_3_out, Cin);
  and and_1 (and_1_out, not_1_out, not_2_out);
  and and_2 (and_2_out, A, B);
  or or_1 (or_1_out, A, B);
  xor xor_1 (xor_1_out, A, B);
  or or_2 (or_2_out, and_1_out, and_2_out);
  and and_3 (and_3_out, or_1_out, Cin);
  or or_3 (Cout, and_3_out, and_4_out);
  and and_4 (and_4_out, A, B);
  and and_5 (and_5_out, xor_1_out, not_3_out);
  or or_4 (Sum, and_5_out, and_6_out);
  and and_6 (and_6_out, Cin, or_2_out);
endmodule

module _12_Bit_Ripple_Carry_Adder (
  input  [11:0] A,
  input  [11:0] B,
  input  Cin,
  output [11:0] Som,
  output Cout,
  output Overflow
);

  wire n1_bit_adder_1_cout, n1_bit_adder_2_cout, n1_bit_adder_3_cout, n1_bit_adder_4_cout,
       n1_bit_adder_5_cout, n1_bit_adder_6_cout, n1_bit_adder_7_cout, n1_bit_adder_8_cout,
       n1_bit_adder_9_cout, n1_bit_adder_10_cout, n1_bit_adder_11_cout;

  _1_Bit_Adder u_1_bit_adder_1 (.A(A[0]), .B(B[0]), .Cin(Cin), .Cout(n1_bit_adder_1_cout), .Sum(Som[0]));
  _1_Bit_Adder u_1_bit_adder_2 (
    .A(A[1]), .B(B[1]), .Cin(n1_bit_adder_1_cout), .Cout(n1_bit_adder_2_cout), .Sum(Som[1]));
  _1_Bit_Adder u_1_bit_adder_3 (
    .A(A[2]), .B(B[2]), .Cin(n1_bit_adder_2_cout), .Cout(n1_bit_adder_3_cout), .Sum(Som[2]));
  _1_Bit_Adder u_1_bit_adder_4 (
    .A(A[3]), .B(B[3]), .Cin(n1_bit_adder_3_cout), .Cout(n1_bit_adder_4_cout), .Sum(Som[3]));
  _1_Bit_Adder u_1_bit_adder_5 (
    .A(B[4]), .B(A[4]), .Cin(n1_bit_adder_4_cout), .Cout(n1_bit_adder_5_cout), .Sum(Som[4]));
  _1_Bit_Adder u_1_bit_adder_6 (
    .A(A[5]), .B(B[5]), .Cin(n1_bit_adder_5_cout), .Cout(n1_bit_adder_6_cout), .Sum(Som[5]));
  _1_Bit_Adder u_1_bit_adder_7 (
    .A(A[6]), .B(B[6]), .Cin(n1_bit_adder_6_cout), .Cout(n1_bit_adder_7_cout), .Sum(Som[6]));
  _1_Bit_Adder u_1_bit_adder_8 (
    .A(A[7]), .B(B[7]), .Cin(n1_bit_adder_7_cout), .Cout(n1_bit_adder_8_cout), .Sum(Som[7]));
  _1_Bit_Adder u_1_bit_adder_9 (
    .A(A[8]), .B(B[8]), .Cin(n1_bit_adder_8_cout), .Cout(n1_bit_adder_9_cout), .Sum(Som[8]));
  _1_Bit_Adder u_1_bit_adder_10 (
    .A(A[9]), .B(B[9]), .Cin(n1_bit_adder_9_cout), .Cout(n1_bit_adder_10_cout), .Sum(Som[9]));
  _1_Bit_Adder u_1_bit_adder_11 (
    .A(A[10]), .B(B[10]), .Cin(n1_bit_adder_10_cout), .Cout(n1_bit_adder_11_cout), .Sum(Som[10]));
  _1_Bit_Adder u_1_bit_adder_12 (.A(A[11]), .B(B[11]), .Cin(n1_bit_adder_11_cout), .Cout(Cout), .Sum(Som[11]));
  xor xor_1 (Overflow, Cout, n1_bit_adder_11_cout);
endmodule
