// Logisim project 1bit_full_adder.circ as structural Verilog
module _1bit_full_adder (
  input  A,
  input  B,
  input  Cin,
  output Cout,
  output Som
);

  wire and_1_out, and_2_out, and_3_out, and_4_out, and_5_out, and_6_out, and_7_out, and_8_out, and_9_out,
       not_1_out, not_2_out, not_3_out, or_1_out, or_2_out;

  not not_1 (not_1_out, A);
  not not_2 (not_2_out, B);
  not not_3 (not_3_out, Cin);
  and and_1 (and_1_out, A, not_2_out);
  and and_2 (and_2_out, not_1_out, B);
  and and_3 (and_3_out, not_1_out, not_2_out);
  and and_4 (and_4_out, A, B);
  and and_5 (and_5_out, B, Cin);
  and and_6 (and_6_out, A, Cin);
  and and_7 (and_7_out, A, B);
  or or_1 (or_1_out, and_1_out, and_2_out);
  and and_8 (and_8_out, not_3_out, or_1_out);
  and and_9 (and_9_out, Cin, or_2_out);
  or or_2 (or_2_out, and_3_out, and_4_out);
  or or_3 (Cout, and_5_out, and_6_out, and_7_out);
  or or_4 (Som, and_8_out, and_9_out);
endmodule

module _12bit_adder (
  input  [11:0] A,
  input  [11:0] B,
  input  Cin,
  output [11:0] Som,
  output Cout,
  output Overflow
);

  wire and_1_out, n1bit_full_adder_1_cout, n1bit_full_adder_2_cout, n1bit_full_adder_3_cout,
       n1bit_full_adder_4_cout, n1bit_full_adder_5_cout, n1bit_full_adder_6_cout, n1bit_full_adder_7_cout,
       n1bit_full_adder_8_cout, n1bit_full_adder_9_cout, n1bit_full_adder_10_cout, n1bit_full_adder_11_cout,
       nand_1_out;

  _1bit_full_adder u_1bit_full_adder_1 (.A(A[0]), .B(B[0]), .Cin(Cin), .Cout(n1bit_full_adder_1_cout), .Som(Som[0]));
  _1bit_full_adder u_1bit_full_adder_2 (
    .A(A[1]), .B(B[1]), .Cin(n1bit_full_adder_1_cout), .Cout(n1bit_full_adder_2_cout), .Som(Som[1]));
  _1bit_full_adder u_1bit_full_adder_3 (
    .A(A[2]), .B(B[2]), .Cin(n1bit_full_adder_2_cout), .Cout(n1bit_full_adder_3_cout), .Som(Som[2]));
  _1bit_full_adder u_1bit_full_adder_4 (
    .A(A[3]), .B(B[3]), .Cin(n1bit_full_adder_3_cout), .Cout(n1bit_full_adder_4_cout), .Som(Som[3]));
  _1bit_full_adder u_1bit_full_adder_5 (
    .A(B[4]), .B(A[4]), .Cin(n1bit_full_adder_4_cout), .Cout(n1bit_full_adder_5_cout), .Som(Som[4]));
  _1bit_full_adder u_1bit_full_adder_6 (
    .A(A[5]), .B(B[5]), .Cin(n1bit_full_adder_5_cout), .Cout(n1bit_full_adder_6_cout), .Som(Som[5]));
  _1bit_full_adder u_1bit_full_adder_7 (
    .A(A[6]), .B(B[6]), .Cin(n1bit_full_adder_6_cout), .Cout(n1bit_full_adder_7_cout), .Som(Som[6]));
  _1bit_full_adder u_1bit_full_adder_8 (
    .A(A[7]), .B(B[7]), .Cin(n1bit_full_adder_7_cout), .Cout(n1bit_full_adder_8_cout), .Som(Som[7]));
  _1bit_full_adder u_1bit_full_adder_9 (
    .A(A[8]), .B(B[8]), .Cin(n1bit_full_adder_8_cout), .Cout(n1bit_full_adder_9_cout), .Som(Som[8]));
  _1bit_full_adder u_1bit_full_adder_10 (
    .A(A[9]), .B(B[9]), .Cin(n1bit_full_adder_9_cout), .Cout(n1bit_full_adder_10_cout), .Som(Som[9]));
  _1bit_full_adder u_1bit_full_adder_11 (
    .A(A[10]), .B(B[10]), .Cin(n1bit_full_adder_10_cout), .Cout(n1bit_full_adder_11_cout), .Som(Som[10]));
  or or_1 (Overflow, Cout, and_1_out);
  _1bit_full_adder u_1bit_full_adder_12 (
    .A(A[11]), .B(B[11]), .Cin(n1bit_full_adder_11_cout), .Cout(Cout), .Som(Som[11]));
  nand nand_1 (nand_1_out, B[11], A[11]);
  and and_1 (and_1_out, Som[11], nand_1_out);
endmodule
