// Logisim project 4-Bit_CLA.circ as structural Verilog
module _1_Bit_Adder (
  input  A,
  input  B,
  input  Cin,
  output Cout,
  output Sum
);

  wire and_1_out, and_2_out, and_3_out, and_4_out, and_5_out, and_6_out, not_1_out, not_2_out, not_3_out,
       or_1_out, or_2_out, xor_1_out;

  not not_1 (not_1_out, A);
  not not_2 (not_2_out, B);
  not not_3 (not_3_out, Cin);
  and and_1 (and_1_out, not_1_out, not_2_out);
  and and_2 (and_2_out, A, B);
  or or_1 (or_1_out, A, B);
  xor xor_1 (xor_1_out, A, B);
  or or_2 (or_2_out, and_1_out, and_2_out);
  and and_3 (and_3_out, or_1_out, Cin);
  or or_3 (Cout, and_3_out, and_4_out);
  and and_4 (and_4_out, A, B);
  and and_5 (and_5_out, xor_1_out, not_3_out);
  or or_4 (Sum, and_5_out, and_6_out);
  and and_6 (and_6_out, Cin, or_2_out);
endmodule

module _4_Bit_Lookaheads (
  input  carryIn,
  input  a0,
  input  a1,
  input  a2,
  input  a3,
  input  b0,
  input  b1,
  input  b2,
  input  b3,
  output c1,
  output c2,
  output c3,
  output c4
);

  wire and_1_out, and_2_out, and_3_out, and_4_out, and_5_out, and_6_out, and_7_out, and_8_out, and_9_out,
       and_10_out, and_11_out, and_12_out, and_13_out, and_14_out, and_15_out, and_16_out, and_17_out,
       and_18_out, and_19_out, and_20_out, and_21_out, and_22_out, and_23_out, and_24_out, and_25_out,
       and_26_out, and_27_out, and_28_out, and_29_out, and_30_out, and_31_out, and_32_out, and_33_out,
       and_34_out, and_35_out, and_36_out, and_37_out, and_38_out, and_39_out, and_40_out, and_41_out,
       and_42_out, and_43_out, and_44_out, and_45_out, and_46_out, and_47_out, and_48_out, and_49_out,
       and_50_out, and_51_out, and_52_out, and_53_out, and_54_out, and_55_out, and_56_out, and_57_out,
       and_58_out, and_59_out, and_60_out, and_61_out, and_62_out, and_63_out, and_64_out, and_65_out,
       and_66_out, and_67_out, and_68_out, and_69_out, and_70_out, and_71_out, and_72_out, and_73_out,
       and_74_out, and_75_out, and_76_out, and_77_out, and_78_out, or_2_out, or_3_out, or_4_out, or_5_out,
       or_6_out, or_7_out, or_8_out, or_9_out, or_10_out, or_11_out, or_12_out, or_13_out, or_14_out,
       or_15_out, or_17_out, or_18_out, or_19_out, or_20_out, or_21_out, or_22_out, or_24_out, or_25_out;

  and and_1 (and_1_out, a0, carryIn);
  and and_2 (and_2_out, b0, carryIn);
  and and_3 (and_3_out, a0, b0);
  and and_4 (and_4_out, a0, carryIn);
  and and_5 (and_5_out, b0, carryIn);
  and and_6 (and_6_out, a0, b0);
  and and_7 (and_7_out, a0, carryIn);
  and and_8 (and_8_out, b0, carryIn);
  and and_9 (and_9_out, a0, b0);
  and and_10 (and_10_out, a0, carryIn);
  and and_11 (and_11_out, b0, carryIn);
  and and_12 (and_12_out, a0, b0);
  and and_13 (and_13_out, a0, carryIn);
  and and_14 (and_14_out, b0, carryIn);
  and and_15 (and_15_out, a0, b0);
  and and_16 (and_16_out, a0, carryIn);
  and and_17 (and_17_out, b0, carryIn);
  and and_18 (and_18_out, a0, b0);
  and and_19 (and_19_out, a0, carryIn);
  and and_20 (and_20_out, b0, carryIn);
  and and_21 (and_21_out, a0, b0);
  and and_22 (and_22_out, a0, carryIn);
  and and_23 (and_23_out, b0, carryIn);
  and and_24 (and_24_out, a0, b0);
  and and_25 (and_25_out, a0, carryIn);
  and and_26 (and_26_out, b0, carryIn);
  and and_27 (and_27_out, a0, b0);
  and and_28 (and_28_out, a0, carryIn);
  and and_29 (and_29_out, b0, carryIn);
  and and_30 (and_30_out, a0, b0);
  and and_31 (and_31_out, a0, carryIn);
  and and_32 (and_32_out, b0, carryIn);
  and and_33 (and_33_out, a0, b0);
  and and_34 (and_34_out, a0, carryIn);
  and and_35 (and_35_out, b0, carryIn);
  and and_36 (and_36_out, a0, b0);
  and and_37 (and_37_out, a0, carryIn);
  and and_38 (and_38_out, b0, carryIn);
  and and_39 (and_39_out, a0, b0);
  and and_40 (and_40_out, a0, carryIn);
  and and_41 (and_41_out, b0, carryIn);
  and and_42 (and_42_out, a0, b0);
  and and_43 (and_43_out, a0, carryIn);
  and and_44 (and_44_out, b0, carryIn);
  and and_45 (and_45_out, a0, b0);
  or or_1 (c1, and_1_out, and_2_out, and_3_out);
  or or_2 (or_2_out, and_4_out, and_5_out, and_6_out);
  or or_3 (or_3_out, and_7_out, and_8_out, and_9_out);
  or or_4 (or_4_out, and_10_out, and_11_out, and_12_out);
  or or_5 (or_5_out, and_13_out, and_14_out, and_15_out);
  or or_6 (or_6_out, and_16_out, and_17_out, and_18_out);
  or or_7 (or_7_out, and_19_out, and_20_out, and_21_out);
  or or_8 (or_8_out, and_22_out, and_23_out, and_24_out);
  or or_9 (or_9_out, and_25_out, and_26_out, and_27_out);
  or or_10 (or_10_out, and_28_out, and_29_out, and_30_out);
  or or_11 (or_11_out, and_31_out, and_32_out, and_33_out);
  or or_12 (or_12_out, and_34_out, and_35_out, and_36_out);
  or or_13 (or_13_out, and_37_out, and_38_out, and_39_out);
  or or_14 (or_14_out, and_40_out, and_41_out, and_42_out);
  or or_15 (or_15_out, and_43_out, and_44_out, and_45_out);
  and and_46 (and_46_out, a1, or_2_out);
  and and_47 (and_47_out, b1, or_3_out);
  and and_48 (and_48_out, a1, b1);
  and and_49 (and_49_out, a1, or_4_out);
  and and_50 (and_50_out, b1, or_5_out);
  and and_51 (and_51_out, a1, b1);
  and and_52 (and_52_out, a1, or_6_out);
  and and_53 (and_53_out, b1, or_7_out);
  and and_54 (and_54_out, a1, b1);
  and and_55 (and_55_out, a1, or_8_out);
  and and_56 (and_56_out, b1, or_9_out);
  and and_57 (and_57_out, a1, b1);
  and and_58 (and_58_out, a1, or_10_out);
  and and_59 (and_59_out, b1, or_11_out);
  and and_60 (and_60_out, a1, b1);
  and and_61 (and_61_out, a1, or_12_out);
  and and_62 (and_62_out, b1, or_13_out);
  and and_63 (and_63_out, a1, b1);
  and and_64 (and_64_out, a1, or_14_out);
  and and_65 (and_65_out, b1, or_15_out);
  and and_66 (and_66_out, a1, b1);
  or or_16 (c2, and_46_out, and_47_out, and_48_out);
  and and_67 (and_67_out, a2, or_17_out);
  or or_17 (or_17_out, and_49_out, and_50_out, and_51_out);
  and and_68 (and_68_out, b2, or_18_out);
  or or_18 (or_18_out, and_52_out, and_53_out, and_54_out);
  and and_69 (and_69_out, a2, b2);
  and and_70 (and_70_out, a2, or_19_out);
  or or_19 (or_19_out, and_55_out, and_56_out, and_57_out);
  and and_71 (and_71_out, b2, or_20_out);
  or or_20 (or_20_out, and_58_out, and_59_out, and_60_out);
  and and_72 (and_72_out, a2, b2);
  and and_73 (and_73_out, a2, or_21_out);
  or or_21 (or_21_out, and_61_out, and_62_out, and_63_out);
  and and_74 (and_74_out, b2, or_22_out);
  or or_22 (or_22_out, and_64_out, and_65_out, and_66_out);
  and and_75 (and_75_out, a2, b2);
  or or_23 (c3, and_67_out, and_68_out, and_69_out);
  or or_24 (or_24_out, and_70_out, and_71_out, and_72_out);
  or or_25 (or_25_out, and_73_out, and_74_out, and_75_out);
  and and_76 (and_76_out, a3, or_24_out);
  and and_77 (and_77_out, b3, or_25_out);
  and and_78 (and_78_out, a3, b3);
  or or_26 (c4, and_76_out, and_77_out, and_78_out);
endmodule

module _4_Bit_Generate_Propagate (
  input  b3,
  input  b2,
  input  b1,
  input  b0,
  input  a3,
  input  a2,
  input  a1,
  input  a0,
  output P,
  output G
);

  wire and_1_out, and_2_out, and_3_out, and_4_out, and_5_out, and_6_out, and_8_out, or_1_out, or_2_out,
       or_4_out, or_5_out;

  or or_1 (or_1_out, a3, b3);
  and and_1 (and_1_out, a3, b3);
  and and_2 (and_2_out, and_3_out, or_1_out);
  and and_3 (and_3_out, a2, b2);
  or or_2 (or_2_out, a2, b2);
  and and_4 (and_4_out, or_1_out, or_2_out, and_6_out);
  and and_5 (and_5_out, or_1_out, or_2_out, or_4_out, and_8_out);
  or or_3 (G, and_1_out, and_2_out, and_4_out, and_5_out);
  or or_4 (or_4_out, a1, b1);
  and and_6 (and_6_out, a1, b1);
  and and_7 (P, or_1_out, or_2_out, or_4_out, or_5_out);
  or or_5 (or_5_out, a0, b0);
  and and_8 (and_8_out, a0, b0);
endmodule

module _4_Bit_CLA (
  input  b3,
  input  b2,
  input  b1,
  input  b0,
  input  a3,
  input  a2,
  input  a1,
  input  a0,
  input  carryIn,
  output s3,
  output s2,
  output s1,
  output s0,
  output G0,
  output P0
);

  wire n4_bit_lookaheads_1_c1, n4_bit_lookaheads_1_c2, n4_bit_lookaheads_1_c3;

  _4_Bit_Generate_Propagate u_4_bit_generate_propagate_1 (
    .b3(b3), .b2(b2), .b1(b1), .b0(b0), .a3(a3), .a2(a2), .a1(a1), .a0(a0), .G(G0), .P(P0));
  _1_Bit_Adder u_1_bit_adder_1 (.A(a3), .B(b3), .Cin(n4_bit_lookaheads_1_c3), .Sum(s3));  // open: Cout
  _1_Bit_Adder u_1_bit_adder_2 (.A(a2), .B(b2), .Cin(n4_bit_lookaheads_1_c2), .Sum(s2));  // open: Cout
  _4_Bit_Lookaheads u_4_bit_lookaheads_1 (
    .carryIn(carryIn), .a0(a0), .a1(a1), .a2(a2), .a3(a3), .b0(b0), .b1(b1), .b2(b2), .b3(b3),
    .c1(n4_bit_lookaheads_1_c1), .c2(n4_bit_lookaheads_1_c2), .c3(n4_bit_lookaheads_1_c3));  // open: c4
  _1_Bit_Adder u_1_bit_adder_3 (.A(a1), .B(b1), .Cin(n4_bit_lookaheads_1_c1), .Sum(s1));  // open: Cout
  _1_Bit_Adder u_1_bit_adder_4 (.A(a0), .B(b0), .Cin(carryIn), .Sum(s0));  // open: Cout
endmodule
