// Logisim project 4-Bit_CLA_Gen_Prop.circ as structural Verilog
module _1_Bit_Adder (
  input  A,
  input  B,
  input  Cin,
  output Cout,
  output Sum
);

  wire and_1_out, and_2_out, and_3_out, and_4_out, and_5_out, and_6_out, not_1_out, not_2_out, not_3_out,
       or_1_out, or_2_out, xor_1_out;

  not not_1 (not_1_out, A);
  not not_2 (not_2_out, B);
  not not_3 (not_3_out, Cin);
  and and_1 (and_1_out, not_1_out, not_2_out);
  and and_2 (and_2_out, A, B);
  or or_1 (or_1_out, A, B);
  xor xor_1 (xor_1_out, A, B);
  or or_2 (or_2_out, and_1_out, and_2_out);
  and and_3 (and_3_out, or_1_out, Cin);
  or or_3 (Cout, and_3_out, and_4_out);
  and and_4 (and_4_out, A, B);
  and and_5 (and_5_out, xor_1_out, not_3_out);
  or or_4 (Sum, and_5_out, and_6_out);
  and and_6 (and_6_out, Cin, or_2_out);
endmodule

module _4_Bit_Lookaheads (
  input  carryIn,
  input  a0,
  input  a1,
  input  a2,
  input  a3,
  input  b0,
  input  b1,
  input  b2,
  input  b3,
  output c1,
  output c2,
  output c3,
  output P,
  output G
);

  wire and_1_out, and_2_out, and_3_out, and_4_out, and_5_out, and_6_out, and_7_out, and_8_out, and_9_out,
       and_10_out, and_11_out, and_12_out, and_13_out, or_1_out, or_2_out, or_3_out, or_4_out;

  and and_1 (and_1_out, a0, b0);
  and and_2 (and_2_out, a1, b1);
  and and_3 (and_3_out, a2, b2);
  and and_4 (and_4_out, a3, b3);
  or or_1 (or_1_out, a0, b0);
  or or_2 (or_2_out, a1, b1);
  or or_3 (or_3_out, a2, b2);
  or or_4 (or_4_out, a3, b3);
  and and_5 (and_5_out, or_4_out, or_3_out, and_2_out);
  and and_6 (and_6_out, or_4_out, or_3_out, or_2_out, and_1_out);
  and and_7 (and_7_out, or_1_out, carryIn);
  and and_8 (and_8_out, or_2_out, and_1_out);
  and and_9 (and_9_out, or_2_out, or_1_out, carryIn);
  and and_10 (and_10_out, or_3_out, and_2_out);
  and and_11 (and_11_out, or_3_out, or_2_out, and_1_out);
  and and_12 (and_12_out, or_3_out, or_2_out, or_1_out, carryIn);
  and and_13 (and_13_out, or_4_out, and_3_out);
  or or_5 (c1, and_1_out, and_7_out);
  or or_6 (c2, and_2_out, and_8_out, and_9_out);
  or or_7 (c3, and_3_out, and_10_out, and_11_out, and_12_out);
  and and_14 (P, or_1_out, or_2_out, or_3_out, or_4_out);
  or or_8 (G, and_4_out, and_13_out, and_5_out, and_6_out);
endmodule

module _4_Bit_CLA (
  input  b3,
  input  b2,
  input  b1,
  input  b0,
  input  a3,
  input  a2,
  input  a1,
  input  a0,
  input  carryIn,
  output G0,
  output P0,
  output s3,
  output s2,
  output s1,
  output s0
);

  wire n4_bit_lookaheads_1_c1, n4_bit_lookaheads_1_c2, n4_bit_lookaheads_1_c3;

  _1_Bit_Adder u_1_bit_adder_1 (.A(a3), .B(b3), .Cin(n4_bit_lookaheads_1_c3), .Sum(s3));  // open: Cout
  _1_Bit_Adder u_1_bit_adder_2 (.A(a2), .B(b2), .Cin(n4_bit_lookaheads_1_c2), .Sum(s2));  // open: Cout
  _4_Bit_Lookaheads u_4_bit_lookaheads_1 (
    .carryIn(carryIn), .a0(a0), .a1(a1), .a2(a2), .a3(a3), .b0(b0), .b1(b1), .b2(b2), .b3(b3),
    .c1(n4_bit_lookaheads_1_c1), .c2(n4_bit_lookaheads_1_c2), .c3(n4_bit_lookaheads_1_c3), .P(P0), .G(G0));
  _1_Bit_Adder u_1_bit_adder_3 (.A(a1), .B(b1), .Cin(n4_bit_lookaheads_1_c1), .Sum(s1));  // open: Cout
  _1_Bit_Adder u_1_bit_adder_4 (.A(a0), .B(b0), .Cin(carryIn), .Sum(s0));  // open: Cout
endmodule
