// Logisim project adder.circ as structural Verilog
module _1bit_full_adder (
  input  A,
  input  B,
  input  Cin,
  output Cout,
  output Som
);

  wire and_1_out, and_2_out, and_3_out, and_4_out, and_5_out, and_6_out, and_7_out, not_1_out, not_2_out,
       not_3_out;

  not not_1 (not_1_out, A);
  not not_2 (not_2_out, B);
  not not_3 (not_3_out, Cin);
  and and_1 (and_1_out, B, Cin);
  and and_2 (and_2_out, A, Cin);
  and and_3 (and_3_out, A, B);
  and and_4 (and_4_out, A, not_2_out, not_3_out);
  and and_5 (and_5_out, not_1_out, B, not_3_out);
  and and_6 (and_6_out, not_1_out, not_2_out, Cin);
  and and_7 (and_7_out, A, B, Cin);
  or or_1 (Cout, and_1_out, and_2_out, and_3_out);
  or or_2 (Som, and_4_out, and_5_out, and_6_out, and_7_out);
endmodule

module _4bit_adder (
  input  b3,
  input  b2,
  input  b1,
  input  b0,
  input  a3,
  input  a2,
  input  a1,
  input  a0,
  input  carryIn,
  output s3,
  output s2,
  output s1,
  output s0,
  output overflow,
  output G0,
  output P0
);

  wire n1bit_full_adder_1_cout, n4bit_lookaheads_with_generate_propagate_1_c1,
       n4bit_lookaheads_with_generate_propagate_1_c2, n4bit_lookaheads_with_generate_propagate_1_c3;

  xor xor_1 (overflow, n1bit_full_adder_1_cout, n4bit_lookaheads_with_generate_propagate_1_c3);
  _4bit_generate_propagate u_4bit_generate_propagate_1 (
    .b3(b3), .b2(b2), .b1(b1), .b0(b0), .a3(a3), .a2(a2), .a1(a1), .a0(a0), .G(G0), .P(P0));
  _1bit_full_adder u_1bit_full_adder_1 (
    .A(a3), .B(b3), .Cin(n4bit_lookaheads_with_generate_propagate_1_c3), .Cout(n1bit_full_adder_1_cout),
    .Som(s3));
  _1bit_full_adder u_1bit_full_adder_2 (
    .A(a2), .B(b2), .Cin(n4bit_lookaheads_with_generate_propagate_1_c2), .Som(s2));  // open: Cout
  _4bit_lookaheads_with_generate_propagate u_4bit_lookaheads_with_generate_propagate_1 (
    .carryIn(carryIn), .a0(a0), .a1(a1), .a2(a2), .a3(a3), .b0(b0), .b1(b1), .b2(b2), .b3(b3),
    .c1(n4bit_lookaheads_with_generate_propagate_1_c1), .c2(n4bit_lookaheads_with_generate_propagate_1_c2),
    .c3(n4bit_lookaheads_with_generate_propagate_1_c3));  // open: c4
  _1bit_full_adder u_1bit_full_adder_3 (
    .A(a1), .B(b1), .Cin(n4bit_lookaheads_with_generate_propagate_1_c1), .Som(s1));  // open: Cout
  _1bit_full_adder u_1bit_full_adder_4 (.A(a0), .B(b0), .Cin(carryIn), .Som(s0));  // open: Cout
endmodule

// carries
module _4bit_lookaheads (
  input  carryIn,
  input  a0,
  input  a1,
  input  a2,
  input  a3,
  input  b0,
  input  b1,
  input  b2,
  input  b3,
  output c1,
  output c2,
  output c3,
  output c4
);

  wire and_1_out, and_2_out, and_3_out, and_4_out, and_5_out, and_6_out, and_7_out, and_8_out, and_9_out,
       and_10_out, and_11_out, and_12_out, and_13_out, and_14_out, and_15_out, and_16_out, and_17_out,
       and_18_out, and_19_out, and_20_out, and_21_out, and_22_out, and_23_out, and_24_out, and_25_out,
       and_26_out, and_27_out, and_28_out, and_29_out, and_30_out, and_31_out, and_32_out, and_33_out,
       and_34_out, and_35_out, and_36_out, and_37_out, and_38_out, and_39_out, and_40_out, and_41_out,
       and_42_out, and_43_out, and_44_out, and_45_out, and_46_out, and_47_out, and_48_out, and_49_out,
       and_50_out, and_51_out, and_52_out, and_53_out, and_54_out, and_55_out, and_56_out, and_57_out,
       and_58_out, and_59_out, and_60_out, and_61_out, and_62_out, and_63_out, and_64_out, and_65_out,
       and_66_out, and_67_out, and_68_out, and_69_out, and_70_out, and_71_out, and_72_out, and_73_out,
       and_74_out, and_75_out, and_76_out, and_77_out, and_78_out, or_2_out, or_3_out, or_4_out, or_5_out,
       or_6_out, or_7_out, or_8_out, or_9_out, or_10_out, or_11_out, or_12_out, or_13_out, or_14_out,
       or_15_out, or_17_out, or_18_out, or_19_out, or_20_out, or_21_out, or_22_out, or_24_out, or_25_out;

  and and_1 (and_1_out, a0, carryIn);
  and and_2 (and_2_out, b0, carryIn);
  and and_3 (and_3_out, a0, b0);
  and and_4 (and_4_out, a0, carryIn);
  and and_5 (and_5_out, b0, carryIn);
  and and_6 (and_6_out, a0, b0);
  and and_7 (and_7_out, a0, carryIn);
  and and_8 (and_8_out, b0, carryIn);
  and and_9 (and_9_out, a0, b0);
  and and_10 (and_10_out, a0, carryIn);
  and and_11 (and_11_out, b0, carryIn);
  and and_12 (and_12_out, a0, b0);
  and and_13 (and_13_out, a0, carryIn);
  and and_14 (and_14_out, b0, carryIn);
  and and_15 (and_15_out, a0, b0);
  and and_16 (and_16_out, a0, carryIn);
  and and_17 (and_17_out, b0, carryIn);
  and and_18 (and_18_out, a0, b0);
  and and_19 (and_19_out, a0, carryIn);
  and and_20 (and_20_out, b0, carryIn);
  and and_21 (and_21_out, a0, b0);
  and and_22 (and_22_out, a0, carryIn);
  and and_23 (and_23_out, b0, carryIn);
  and and_24 (and_24_out, a0, b0);
  and and_25 (and_25_out, a0, carryIn);
  and and_26 (and_26_out, b0, carryIn);
  and and_27 (and_27_out, a0, b0);
  and and_28 (and_28_out, a0, carryIn);
  and and_29 (and_29_out, b0, carryIn);
  and and_30 (and_30_out, a0, b0);
  and and_31 (and_31_out, a0, carryIn);
  and and_32 (and_32_out, b0, carryIn);
  and and_33 (and_33_out, a0, b0);
  and and_34 (and_34_out, a0, carryIn);
  and and_35 (and_35_out, b0, carryIn);
  and and_36 (and_36_out, a0, b0);
  and and_37 (and_37_out, a0, carryIn);
  and and_38 (and_38_out, b0, carryIn);
  and and_39 (and_39_out, a0, b0);
  and and_40 (and_40_out, a0, carryIn);
  and and_41 (and_41_out, b0, carryIn);
  and and_42 (and_42_out, a0, b0);
  and and_43 (and_43_out, a0, carryIn);
  and and_44 (and_44_out, b0, carryIn);
  and and_45 (and_45_out, a0, b0);
  or or_1 (c1, and_1_out, and_2_out, and_3_out);
  or or_2 (or_2_out, and_4_out, and_5_out, and_6_out);
  or or_3 (or_3_out, and_7_out, and_8_out, and_9_out);
  or or_4 (or_4_out, and_10_out, and_11_out, and_12_out);
  or or_5 (or_5_out, and_13_out, and_14_out, and_15_out);
  or or_6 (or_6_out, and_16_out, and_17_out, and_18_out);
  or or_7 (or_7_out, and_19_out, and_20_out, and_21_out);
  or or_8 (or_8_out, and_22_out, and_23_out, and_24_out);
  or or_9 (or_9_out, and_25_out, and_26_out, and_27_out);
  or or_10 (or_10_out, and_28_out, and_29_out, and_30_out);
  or or_11 (or_11_out, and_31_out, and_32_out, and_33_out);
  or or_12 (or_12_out, and_34_out, and_35_out, and_36_out);
  or or_13 (or_13_out, and_37_out, and_38_out, and_39_out);
  or or_14 (or_14_out, and_40_out, and_41_out, and_42_out);
  or or_15 (or_15_out, and_43_out, and_44_out, and_45_out);
  and and_46 (and_46_out, a1, or_2_out);
  and and_47 (and_47_out, b1, or_3_out);
  and and_48 (and_48_out, a1, b1);
  and and_49 (and_49_out, a1, or_4_out);
  and and_50 (and_50_out, b1, or_5_out);
  and and_51 (and_51_out, a1, b1);
  and and_52 (and_52_out, a1, or_6_out);
  and and_53 (and_53_out, b1, or_7_out);
  and and_54 (and_54_out, a1, b1);
  and and_55 (and_55_out, a1, or_8_out);
  and and_56 (and_56_out, b1, or_9_out);
  and and_57 (and_57_out, a1, b1);
  and and_58 (and_58_out, a1, or_10_out);
  and and_59 (and_59_out, b1, or_11_out);
  and and_60 (and_60_out, a1, b1);
  and and_61 (and_61_out, a1, or_12_out);
  and and_62 (and_62_out, b1, or_13_out);
  and and_63 (and_63_out, a1, b1);
  and and_64 (and_64_out, a1, or_14_out);
  and and_65 (and_65_out, b1, or_15_out);
  and and_66 (and_66_out, a1, b1);
  or or_16 (c2, and_46_out, and_47_out, and_48_out);
  and and_67 (and_67_out, a2, or_17_out);
  or or_17 (or_17_out, and_49_out, and_50_out, and_51_out);
  and and_68 (and_68_out, b2, or_18_out);
  or or_18 (or_18_out, and_52_out, and_53_out, and_54_out);
  and and_69 (and_69_out, a2, b2);
  and and_70 (and_70_out, a2, or_19_out);
  or or_19 (or_19_out, and_55_out, and_56_out, and_57_out);
  and and_71 (and_71_out, b2, or_20_out);
  or or_20 (or_20_out, and_58_out, and_59_out, and_60_out);
  and and_72 (and_72_out, a2, b2);
  and and_73 (and_73_out, a2, or_21_out);
  or or_21 (or_21_out, and_61_out, and_62_out, and_63_out);
  and and_74 (and_74_out, b2, or_22_out);
  or or_22 (or_22_out, and_64_out, and_65_out, and_66_out);
  and and_75 (and_75_out, a2, b2);
  or or_23 (c3, and_67_out, and_68_out, and_69_out);
  or or_24 (or_24_out, and_70_out, and_71_out, and_72_out);
  or or_25 (or_25_out, and_73_out, and_74_out, and_75_out);
  and and_76 (and_76_out, a3, or_24_out);
  and and_77 (and_77_out, b3, or_25_out);
  and and_78 (and_78_out, a3, b3);
  or or_26 (c4, and_76_out, and_77_out, and_78_out);
endmodule

module _1bit_generate_propagate (
  input  a,
  input  b,
  output g,
  output p
);

  and and_1 (g, a, b);
  or or_1 (p, a, b);
endmodule

// Super-Generate & -Propagate
module _4bit_generate_propagate (
  input  b3,
  input  b2,
  input  b1,
  input  b0,
  input  a3,
  input  a2,
  input  a1,
  input  a0,
  output P,
  output G
);

  wire and_1_out, and_2_out, and_3_out, n1bit_generate_propagate_1_g, n1bit_generate_propagate_1_p,
       n1bit_generate_propagate_2_g, n1bit_generate_propagate_2_p, n1bit_generate_propagate_3_g,
       n1bit_generate_propagate_3_p, n1bit_generate_propagate_4_g, n1bit_generate_propagate_4_p;

  _1bit_generate_propagate u_1bit_generate_propagate_1 (
    .a(a3), .b(b3), .g(n1bit_generate_propagate_1_g), .p(n1bit_generate_propagate_1_p));
  and and_1 (and_1_out, n1bit_generate_propagate_2_g, n1bit_generate_propagate_1_p);
  _1bit_generate_propagate u_1bit_generate_propagate_2 (
    .a(a2), .b(b2), .g(n1bit_generate_propagate_2_g), .p(n1bit_generate_propagate_2_p));
  and and_2 (and_2_out, n1bit_generate_propagate_1_p, n1bit_generate_propagate_2_p, n1bit_generate_propagate_3_g);
  and and_3 (and_3_out, n1bit_generate_propagate_1_p, n1bit_generate_propagate_2_p, n1bit_generate_propagate_3_p, n1bit_generate_propagate_4_g);
  or or_1 (G, n1bit_generate_propagate_1_g, and_1_out, and_2_out, and_3_out);
  _1bit_generate_propagate u_1bit_generate_propagate_3 (
    .a(a1), .b(b1), .g(n1bit_generate_propagate_3_g), .p(n1bit_generate_propagate_3_p));
  and and_4 (P, n1bit_generate_propagate_1_p, n1bit_generate_propagate_2_p, n1bit_generate_propagate_3_p, n1bit_generate_propagate_4_p);
  _1bit_generate_propagate u_1bit_generate_propagate_4 (
    .a(a0), .b(b0), .g(n1bit_generate_propagate_4_g), .p(n1bit_generate_propagate_4_p));
endmodule

module _4bit_lookaheads_with_generate_propagate (
  input  carryIn,
  input  a0,
  input  a1,
  input  a2,
  input  a3,
  input  b0,
  input  b1,
  input  b2,
  input  b3,
  output c1,
  output c2,
  output c3,
  output c4
);

  wire and_1_out, and_2_out, and_3_out, and_4_out, and_5_out, and_6_out, and_7_out, and_8_out, and_9_out,
       and_10_out, and_11_out, and_12_out, and_13_out, and_14_out, or_1_out, or_2_out, or_3_out, or_4_out;

  and and_1 (and_1_out, a0, b0);
  and and_2 (and_2_out, a1, b1);
  and and_3 (and_3_out, a2, b2);
  and and_4 (and_4_out, a3, b3);
  or or_1 (or_1_out, a0, b0);
  or or_2 (or_2_out, a1, b1);
  or or_3 (or_3_out, a2, b2);
  or or_4 (or_4_out, a3, b3);
  and and_5 (and_5_out, or_1_out, carryIn);
  and and_6 (and_6_out, or_2_out, and_1_out);
  and and_7 (and_7_out, or_2_out, or_1_out, carryIn);
  and and_8 (and_8_out, or_3_out, and_2_out);
  and and_9 (and_9_out, or_3_out, or_2_out, and_1_out);
  and and_10 (and_10_out, or_3_out, or_2_out, or_1_out, carryIn);
  and and_11 (and_11_out, or_4_out, and_3_out);
  and and_12 (and_12_out, or_4_out, or_3_out, and_2_out);
  and and_13 (and_13_out, or_4_out, or_3_out, or_2_out, and_1_out);
  and and_14 (and_14_out, or_4_out, or_3_out, or_2_out, or_1_out, carryIn);
  or or_5 (c1, and_1_out, and_5_out);
  or or_6 (c2, and_2_out, and_6_out, and_7_out);
  or or_7 (c3, and_3_out, and_8_out, and_9_out, and_10_out);
  or or_8 (c4, and_4_out, and_11_out, and_12_out, and_13_out, and_14_out);
endmodule

module carrylookahead_unit (
  input  carryIn,
  input  P0,
  input  P1,
  input  P2,
  input  G0,
  input  G1,
  input  G2,
  output C1,
  output C2,
  output C3
);

  wire and_1_out, and_2_out, and_3_out, and_4_out, and_5_out, and_6_out;

  or or_1 (C1, G0, and_1_out);
  and and_1 (and_1_out, P0, carryIn);
  or or_2 (C2, G1, and_2_out, and_3_out);
  and and_2 (and_2_out, P1, G0);
  and and_3 (and_3_out, P1, P0, carryIn);
  and and_4 (and_4_out, P2, G1);
  and and_5 (and_5_out, P2, P1, G0);
  and and_6 (and_6_out, P2, P1, P0, carryIn);
  or or_3 (C3, G2, and_4_out, and_5_out, and_6_out);
endmodule

module _12bit_ripplecarry_adder (
  input  [11:0] A,
  input  [11:0] B,
  input  Cin,
  output Cout,
  output [11:0] Som,
  output Overflow
);

  wire n1bit_full_adder_1_cout, n1bit_full_adder_2_cout, n1bit_full_adder_3_cout, n1bit_full_adder_4_cout,
       n1bit_full_adder_5_cout, n1bit_full_adder_6_cout, n1bit_full_adder_7_cout, n1bit_full_adder_8_cout,
       n1bit_full_adder_9_cout, n1bit_full_adder_10_cout, n1bit_full_adder_11_cout;

  _1bit_full_adder u_1bit_full_adder_1 (.A(A[0]), .B(B[0]), .Cin(Cin), .Cout(n1bit_full_adder_1_cout), .Som(Som[0]));
  _1bit_full_adder u_1bit_full_adder_2 (
    .A(A[1]), .B(B[1]), .Cin(n1bit_full_adder_1_cout), .Cout(n1bit_full_adder_2_cout), .Som(Som[1]));
  _1bit_full_adder u_1bit_full_adder_3 (
    .A(A[2]), .B(B[2]), .Cin(n1bit_full_adder_2_cout), .Cout(n1bit_full_adder_3_cout), .Som(Som[2]));
  _1bit_full_adder u_1bit_full_adder_4 (
    .A(A[3]), .B(B[3]), .Cin(n1bit_full_adder_3_cout), .Cout(n1bit_full_adder_4_cout), .Som(Som[3]));
  _1bit_full_adder u_1bit_full_adder_5 (
    .A(B[4]), .B(A[4]), .Cin(n1bit_full_adder_4_cout), .Cout(n1bit_full_adder_5_cout), .Som(Som[4]));
  _1bit_full_adder u_1bit_full_adder_6 (
    .A(A[5]), .B(B[5]), .Cin(n1bit_full_adder_5_cout), .Cout(n1bit_full_adder_6_cout), .Som(Som[5]));
  _1bit_full_adder u_1bit_full_adder_7 (
    .A(A[6]), .B(B[6]), .Cin(n1bit_full_adder_6_cout), .Cout(n1bit_full_adder_7_cout), .Som(Som[6]));
  _1bit_full_adder u_1bit_full_adder_8 (
    .A(A[7]), .B(B[7]), .Cin(n1bit_full_adder_7_cout), .Cout(n1bit_full_adder_8_cout), .Som(Som[7]));
  _1bit_full_adder u_1bit_full_adder_9 (
    .A(A[8]), .B(B[8]), .Cin(n1bit_full_adder_8_cout), .Cout(n1bit_full_adder_9_cout), .Som(Som[8]));
  _1bit_full_adder u_1bit_full_adder_10 (
    .A(A[9]), .B(B[9]), .Cin(n1bit_full_adder_9_cout), .Cout(n1bit_full_adder_10_cout), .Som(Som[9]));
  _1bit_full_adder u_1bit_full_adder_11 (
    .A(A[10]), .B(B[10]), .Cin(n1bit_full_adder_10_cout), .Cout(n1bit_full_adder_11_cout), .Som(Som[10]));
  xor xor_1 (Overflow, n1bit_full_adder_11_cout, Cout);
  _1bit_full_adder u_1bit_full_adder_12 (
    .A(A[11]), .B(B[11]), .Cin(n1bit_full_adder_11_cout), .Cout(Cout), .Som(Som[11]));
endmodule

module _12bit_carry_lookahead (
  input  carryIn,
  input  [11:0] A,
  input  [11:0] B,
  output carryOut,
  output [11:0] Som,
  output Overflow
);

  wire carrylookahead_unit_1_c1, carrylookahead_unit_1_c2, n4bit_adder_1_g0, n4bit_adder_1_p0,
       n4bit_adder_2_g0, n4bit_adder_2_p0, n4bit_adder_3_g0, n4bit_adder_3_p0;

  _4bit_adder u_4bit_adder_1 (
    .b3(B[3]), .b2(B[2]), .b1(B[1]), .b0(B[0]), .a3(A[3]), .a2(A[2]), .a1(A[1]), .a0(A[0]),
    .carryIn(carryIn), .G0(n4bit_adder_1_g0), .P0(n4bit_adder_1_p0), .s3(Som[3]), .s2(Som[2]), .s1(Som[1]),
    .s0(Som[0]));  // open: overflow
  _4bit_adder u_4bit_adder_2 (
    .b3(B[7]), .b2(B[6]), .b1(B[5]), .b0(B[4]), .a3(A[7]), .a2(A[6]), .a1(A[5]), .a0(A[4]),
    .carryIn(carrylookahead_unit_1_c1), .G0(n4bit_adder_2_g0), .P0(n4bit_adder_2_p0), .s3(Som[7]),
    .s2(Som[6]), .s1(Som[5]), .s0(Som[4]));  // open: overflow
  _4bit_adder u_4bit_adder_3 (
    .b3(B[11]), .b2(B[10]), .b1(B[9]), .b0(B[8]), .a3(A[11]), .a2(A[10]), .a1(A[9]), .a0(A[8]),
    .carryIn(carrylookahead_unit_1_c2), .overflow(Overflow), .G0(n4bit_adder_3_g0), .P0(n4bit_adder_3_p0),
    .s3(Som[11]), .s2(Som[10]), .s1(Som[9]), .s0(Som[8]));
  carrylookahead_unit carrylookahead_unit_1 (
    .carryIn(carryIn), .P0(n4bit_adder_1_p0), .P1(n4bit_adder_2_p0), .P2(n4bit_adder_3_p0),
    .G0(n4bit_adder_1_g0), .G1(n4bit_adder_2_g0), .G2(n4bit_adder_3_g0), .C1(carrylookahead_unit_1_c1),
    .C2(carrylookahead_unit_1_c2), .C3(carryOut));
endmodule

module vraag4_test (
  input  CarryIn,
  input  [11:0] B,
  input  [11:0] A,
  output Overflow,
  output Overflow_2,
  output CarryOut,
  output CarryOut_2,
  output [11:0] out_8,
  output [11:0] out_9
);

  _12bit_carry_lookahead u_12bit_carry_lookahead_1 (
    .A(A), .B(B), .carryIn(CarryIn), .carryOut(CarryOut), .Som(out_8), .Overflow(Overflow_2));
  _12bit_ripplecarry_adder u_12bit_ripplecarry_adder_1 (
    .Cin(CarryIn), .A(A), .B(B), .Som(out_9), .Cout(CarryOut_2), .Overflow(Overflow));

  // Notes on the sheet:
  //   Vraag 4: Test of dat de ripple carry and carry lookahead juist optellen en overflow's detecteren
endmodule
