// Logisim project check_RCA_CLA.circ as structural Verilog: 1 circuit, main circuit main
module main (
  input  [11:0] A,
  input  [11:0] B,
  input  carryIn,
  output Overflow,
  output Cout,
  output Cout_2,
  output Overflow_2,
  output [11:0] out_8,
  output [11:0] out_9
);

  _12_Bit_CLA u_12_bit_cla_1 (.A(A), .B(B), .carryIn(carryIn), .carryOut(Cout), .Som(out_8), .Overflow(Overflow));
  _12_Bit_Ripple_Carry_Adder u_12_bit_ripple_carry_adder_1 (
    .Cin(carryIn), .A(A), .B(B), .Som(out_9), .Cout(Cout_2), .Overflow(Overflow_2));
endmodule
