// Logisim project ALU_Group50.circ as structural Verilog: 5 circuits, main circuit main
module main (
  output halt,
  output [12:0] counter,
  output [3:0] op,
  output [11:0] a,
  output [11:0] b,
  output [11:0] oracle,
  output [11:0] result,
  output err_oracle,
  output error,
  output ok,
  output start_delimiter
);

  wire and_1_out, and_2_out, clock_1_out, comparator_1_eq, comparator_2_eq;

  Clock clock_1 (.out(clock_1_out));
  Counter #(.width(13), .max('h1fff), .trigger("falling")) counter_1 (
    .Q(counter), .carry(halt), .clk(clock_1_out));  // open: load, D, count, clr
  RAM #(.addrWidth(16), .dataWidth(4), .bus("separate")) ram_1 (
    .addr({counter, 3'b000}), .data(op), .ld(1'b1));  // open: din, str, sel, clk, clr
  RAM #(.addrWidth(16), .dataWidth(12), .bus("separate")) ram_2 (
    .addr({counter, 3'b001}), .data(a), .ld(1'b1));  // open: din, str, sel, clk, clr
  RAM #(.addrWidth(16), .dataWidth(12), .bus("separate")) ram_3 (
    .addr({counter, 3'b010}), .data(b), .ld(1'b1));  // open: din, str, sel, clk, clr
  RAM #(.addrWidth(16), .dataWidth(12), .bus("separate")) ram_4 (
    .addr({counter, 3'b011}), .data(oracle), .ld(1'b1));  // open: din, str, sel, clk, clr
  RAM #(.addrWidth(16), .dataWidth(1), .bus("separate")) ram_5 (
    .addr({counter, 3'b100}), .data(err_oracle), .ld(1'b1));  // open: din, str, sel, clk, clr
  RAM #(.addrWidth(16), .dataWidth(1), .bus("separate")) ram_6 (
    .addr({counter, 3'b101}), .data(start_delimiter), .ld(1'b1));  // open: din, str, sel, clk, clr
  _12_bit_ALU u_12_bit_alu_1 (.ALU_code(op), .a(a), .b(b), .overflow(error), .result(result));
  Comparator #(.width(1), .mode("unsigned")) comparator_1 (
    .a(error), .b(err_oracle), .eq(comparator_1_eq));  // open: gt, lt
  Comparator #(.width(12)) comparator_2 (.a(result), .b(oracle), .eq(comparator_2_eq));  // open: gt, lt
  and and_1 (and_1_out, comparator_1_eq, error);
  and and_2 (and_2_out, comparator_2_eq, comparator_1_eq, ~error);  // AND_Gate
  or or_1 (ok, and_1_out, and_2_out);

  // Notes on the sheet:
  //   You must complete the circuit '12-bit ALU' instead.
  //   DO NOT EDIT THIS CIRCUIT!
endmodule

module _12_bit_ALU (
  input  [3:0] ALU_code,
  input  [11:0] a,
  input  [11:0] b,
  output [11:0] result,
  output overflow
);

  wire Add_overflow, invert_1_overflow, invert_2_overflow, n12_bit_cla_1_overflow, shift_ops_1_sla_overflow,
       shift_ops_1_sra_overflow, xor_1_out;
  wire [11:0] Add_som, AND_out, compare_1_eq, compare_1_gt, compare_1_lt, compare_1_neq, invert_1_result,
       invert_2_result, n12_bit_cla_1_som, Not_out, OR_out, shift_ops_1_sla, shift_ops_1_sll,
       shift_ops_1_sra, shift_ops_1_srl;

  invert invert_1 (.a(b), .result(invert_1_result), .overflow(invert_1_overflow));
  invert invert_2 (.a(a), .result(invert_2_result), .overflow(invert_2_overflow));
  shift_ops shift_ops_1 (
    .a(a), .sll(shift_ops_1_sll), .srl(shift_ops_1_srl), .sla(shift_ops_1_sla), .sra(shift_ops_1_sra),
    .sla_overflow(shift_ops_1_sla_overflow), .sra_overflow(shift_ops_1_sra_overflow));
  _12_Bit_CLA u_12_bit_cla_1 (
    .A(a), .B(invert_1_result), .carryIn(1'b0), .Som(n12_bit_cla_1_som), .Overflow(n12_bit_cla_1_overflow));  // open: carryOut
  _12_Bit_CLA Add (.A(a), .B(b), .carryIn(1'b0), .Som(Add_som), .Overflow(Add_overflow));  // open: carryOut
  assign AND_out = a & b;  // AND_Gate AND, 12 bits wide
  assign OR_out = a | b;  // OR_Gate OR, 12 bits wide
  compare compare_1 (.a(a), .b(b), .lt(compare_1_lt), .gt(compare_1_gt), .eq(compare_1_eq), .neq(compare_1_neq));
  xor xor_1 (xor_1_out, n12_bit_cla_1_overflow, invert_1_overflow);
  assign Not_out = ~a;  // NOT_Gate Not, 12 bits wide
  Multiplexer #(.select(4), .width(12)) multiplexer_1 (
    .in0({12{1'b0}}), .in1(Not_out), .in2(AND_out), .in3(OR_out), .in4(Add_som), .in5(n12_bit_cla_1_som),
    .in6(compare_1_lt), .in7(compare_1_gt), .in8(compare_1_eq), .in9(compare_1_neq), .in10(invert_2_result),
    .in11(shift_ops_1_sll), .in12(shift_ops_1_srl), .in13(shift_ops_1_sla), .in14(shift_ops_1_sra), .in15(a),
    .out(result), .sel(ALU_code));  // open: en
  Multiplexer #(.select(4)) multiplexer_2 (
    .in0(1'b0), .in1(1'b0), .in2(1'b0), .in3(1'b0), .in4(Add_overflow), .in5(xor_1_out), .in6(1'b0),
    .in7(1'b0), .in8(1'b0), .in9(1'b0), .in10(invert_2_overflow), .in11(1'b0), .in12(1'b0),
    .in13(shift_ops_1_sla_overflow), .in14(shift_ops_1_sra_overflow), .in15(1'b0), .out(overflow),
    .sel(ALU_code));  // open: en

  // Notes on the sheet:
  //   This circuit is used as a block in the main circuit, and its layout must remain unchanged. The circuit called "main" should be the main circuit of this file.
  //   Do not change the circuit appearance.
  //   DO NOT CHANGE THE INPUTS AND OUTPUTS OF THIS CIRCUIT!
  //   Do not add/remove inputs or outputs. Do not even change their location or orientation.
endmodule

module invert (
  input  [11:0] a,
  output [11:0] result,
  output overflow
);

  wire [11:0] not_1_out;

  assign not_1_out = ~a;  // NOT_Gate not_1, 12 bits wide
  _12_Bit_CLA u_12_bit_cla_1 (
    .A(not_1_out), .B(12'h1), .carryIn(1'b0), .Som(result), .Overflow(overflow));  // open: carryOut
endmodule

module compare (
  input  [11:0] a,
  input  [11:0] b,
  output [11:0] lt,
  output [11:0] gt,
  output [11:0] eq,
  output [11:0] neq
);

  wire and_1_out, and_2_out, bitselector_1_out, bitselector_2_out, invert_1_overflow, n12_bit_cla_1_overflow,
       nor_1_out, not_1_out, not_2_out, not_3_out, xor_1_out, xor_2_out;
  wire [11:0] invert_1_result, n12_bit_cla_1_som;

  invert invert_1 (.a(b), .result(invert_1_result), .overflow(invert_1_overflow));
  BitSelector #(.width(12)) bitselector_1 (.in(a), .out(bitselector_1_out), .sel(4'b1011));
  BitSelector #(.width(12)) bitselector_2 (.in(b), .out(bitselector_2_out), .sel(4'b1011));
  _12_Bit_CLA u_12_bit_cla_1 (
    .A(a), .B(invert_1_result), .carryIn(1'b0), .Som(n12_bit_cla_1_som), .Overflow(n12_bit_cla_1_overflow));  // open: carryOut
  xor xor_1 (xor_1_out, bitselector_1_out, bitselector_2_out);
  xor xor_2 (xor_2_out, n12_bit_cla_1_overflow, n12_bit_cla_1_som[11]);
  nor nor_1 (nor_1_out, n12_bit_cla_1_som[0], n12_bit_cla_1_som[1], n12_bit_cla_1_som[2], n12_bit_cla_1_som[3], n12_bit_cla_1_som[4], n12_bit_cla_1_som[5], n12_bit_cla_1_som[6], n12_bit_cla_1_som[7], n12_bit_cla_1_som[8], n12_bit_cla_1_som[9], n12_bit_cla_1_som[10], n12_bit_cla_1_som[11]);
  not not_1 (not_1_out, nor_1_out);
  not not_2 (not_2_out, invert_1_overflow);
  not not_3 (not_3_out, and_1_out);
  and and_1 (and_1_out, xor_2_out, not_2_out, not_1_out);
  and and_2 (and_2_out, not_3_out, not_1_out);
  assign lt = {{11{1'b0}}, and_1_out};  // Bit_Extender bit_extender_1
  assign gt = {{11{1'b0}}, and_2_out};  // Bit_Extender bit_extender_2
  assign eq = {{11{1'b0}}, nor_1_out};  // Bit_Extender bit_extender_3
  assign neq = {{11{1'b0}}, not_1_out};  // Bit_Extender bit_extender_4
endmodule

module shift_ops (
  input  [11:0] a,
  output [11:0] sll,
  output [11:0] srl,
  output [11:0] sla,
  output [11:0] sra,
  output sla_overflow,
  output sra_overflow
);

  wire and_1_out, and_2_out, and_3_out, not_1_out, not_2_out, not_3_out;

  not not_1 (not_1_out, a[11]);
  and and_1 (and_1_out, not_1_out, a[0]);
  and and_2 (and_2_out, a[9], not_2_out);
  not not_2 (not_2_out, a[10]);
  and and_3 (and_3_out, a[11], a[11]);
  or or_1 (sla_overflow, and_1_out, and_2_out);
  and and_4 (sra_overflow, a[0], and_3_out, not_3_out);
  not not_3 (not_3_out, a[11]);

  assign sla = {a[10:0], 1'b0};
  assign sll = {a[10:0], 1'b0};
  assign sra = {{2{a[11]}}, a[10:1]};
  assign srl = {1'b0, a[11:1]};
endmodule
