// Logisim project SD_Group05.circ as structural Verilog: 6 circuits, main circuit main
module main (
  output [11:0] pc,
  output [11:0] r0,
  output [11:0] r1,
  output [11:0] r2,
  output [11:0] r3,
  output [11:0] r4,
  output [11:0] r5,
  output [11:0] r6,
  output [11:0] r7,
  output halt
);

  wire and_1_out, clock_1_out, controller_1_alusrc, controller_1_alusrcb, controller_1_memread,
       controller_1_memtoreg, controller_1_memwrite, controller_1_readrd, controller_1_regwrite, not_1_out,
       reset_out;
  wire [2:0] decoder_1_rd, decoder_1_rs, decoder_1_rt, multiplexer_1_out;
  wire [3:0] controller_1_alu_op, decoder_1_func, decoder_1_op_code;
  wire [11:0] decoder_1_imm, multiplexer_2_out, multiplexer_3_out, multiplexer_4_out, n12_bit_alu_1_result,
       ram_2_data, register_file_1_r, register_file_1_s;
  wire [15:0] ram_1_data;

  Halt halt_1 (.instruction(ram_1_data), .clock(clock_1_out), .reset(reset_out), .halt(halt));
  Clock clock_1 (.out(clock_1_out));
  Button reset (.out(reset_out));
  and and_1 (and_1_out, ~halt, clock_1_out);  // AND_Gate
  not not_1 (not_1_out, 1'b0);
  PC pc_1 (
    .branch_rel(1'b0), .branch_abs(1'b0), .branch_val({12{1'b0}}), .C(and_1_out), .reset(reset_out),
    .instruction_address(pc));
  decoder decoder_1 (
    .instruction(ram_1_data), .rt(decoder_1_rt), .func(decoder_1_func), .rs(decoder_1_rs), .rd(decoder_1_rd),
    .op_code(decoder_1_op_code), .imm(decoder_1_imm));
  RAM #(.addrWidth(12), .dataWidth(16)) ram_1 (
    .addr(pc), .data(ram_1_data), .clk(and_1_out), .ld(not_1_out));  // open: sel, clr
  controller controller_1 (
    .op_code(decoder_1_op_code), .func(decoder_1_func), .ALU_op(controller_1_alu_op),
    .RegWrite(controller_1_regwrite), .ALUSrc(controller_1_alusrc), .ALUSrcB(controller_1_alusrcb),
    .MemRead(controller_1_memread), .MemToReg(controller_1_memtoreg), .MemWrite(controller_1_memwrite),
    .ReadRD(controller_1_readrd));  // open: BranchRel, BranchAbs
  Multiplexer #(.width(3), .enable("false")) multiplexer_1 (
    .in0(decoder_1_rt), .in1(decoder_1_rd), .out(multiplexer_1_out), .sel(controller_1_readrd));
  register_file register_file_1 (
    .Data(multiplexer_4_out), .write(controller_1_regwrite), .R(register_file_1_r), .S(register_file_1_s),
    .r1(r1), .r2(r2), .r3(r3), .r4(r4), .rd(decoder_1_rd), .r5(r5), .r6(r6), .r7(r7), .rt(multiplexer_1_out),
    .rs(decoder_1_rs), .clock(and_1_out), .reset(reset_out), .r0(r0));
  Multiplexer #(.width(12), .enable("false")) multiplexer_2 (
    .in0(register_file_1_s), .in1(decoder_1_imm), .out(multiplexer_2_out), .sel(controller_1_alusrc));
  Multiplexer #(.width(12), .enable("false")) multiplexer_3 (
    .in0(register_file_1_r), .in1(decoder_1_imm), .out(multiplexer_3_out), .sel(controller_1_alusrcb));
  _12_bit_ALU u_12_bit_alu_1 (
    .ALU_code(controller_1_alu_op), .a(multiplexer_2_out), .b(multiplexer_3_out),
    .result(n12_bit_alu_1_result));  // open: overflow
  Multiplexer #(.width(12), .enable("false")) multiplexer_4 (
    .in0(n12_bit_alu_1_result), .in1(ram_2_data), .out(multiplexer_4_out), .sel(controller_1_memtoreg));
  RAM #(.addrWidth(12), .dataWidth(12), .bus("separate")) ram_2 (
    .addr(n12_bit_alu_1_result), .din(register_file_1_r), .data(ram_2_data), .str(controller_1_memwrite),
    .clk(and_1_out), .ld(controller_1_memread), .clr(reset_out));  // open: sel

  // Notes on the sheet:
  //   current instruction
  //   clock signal
  //   reset button
  //   DO NOT CHANGE THE INPUTS AND OUTPUTS OF THIS CIRCUIT! Do not add/remove inputs or outputs. Do not even change their location or orientation.
endmodule

module Halt (
  input  [15:0] instruction,
  input  clock,
  input  reset,
  output halt
);

  wire and_1_out, comparator_1_eq, comparator_2_gt, counter_1_carry, or_1_out, or_2_out;
  wire [11:0] counter_1_q;

  Comparator #(.width(16), .mode("unsigned")) comparator_1 (
    .a(instruction), .b({16{1'b0}}), .eq(comparator_1_eq));  // open: gt, lt
  Counter #(.width(12), .max('hfff), .trigger("falling")) counter_1 (
    .Q(counter_1_q), .carry(counter_1_carry), .clk(clock), .clr(reset));  // open: load, D, count
  or or_1 (or_1_out, comparator_1_eq, counter_1_carry);
  Comparator #(.width(12), .mode("unsigned")) comparator_2 (
    .a(counter_1_q), .b({12{1'b0}}), .gt(comparator_2_gt));  // open: eq, lt
  or or_2 (or_2_out, halt, and_1_out);
  and and_1 (and_1_out, or_1_out, comparator_2_gt);
  Register #(.width(1)) register_1 (.D(or_2_out), .Q(halt), .clk(clock), .clr(reset));  // open: en

  // Notes on the sheet:
  //   halt becomes and stays asserted if the instruction is 0000 (not in the first clock cycle) or the end of the counter is reached (2^12)
endmodule

module PC (
  input  branch_rel,
  input  branch_abs,
  input  [11:0] branch_val,
  input  C,
  input  reset,
  output [11:0] instruction_address
);

  wire nor_1_out;
  wire [11:0] bit_extender_1_out, multiplexer_1_out, multiplexer_2_out, n12_bit_cla_1_som, n12_bit_cla_2_som;

  assign bit_extender_1_out = {{11{1'b0}}, 1'b1};  // Bit_Extender bit_extender_1
  _12_Bit_CLA u_12_bit_cla_1 (
    .A(bit_extender_1_out), .B(instruction_address), .carryIn(1'b0), .Som(n12_bit_cla_1_som));  // open: carryOut, Overflow
  _12_Bit_CLA u_12_bit_cla_2 (
    .A(branch_val), .B(instruction_address), .carryIn(1'b1), .Som(n12_bit_cla_2_som));  // open: carryOut, Overflow
  Multiplexer #(.width(12), .enable("false")) multiplexer_1 (
    .in0(n12_bit_cla_2_som), .in1(branch_val), .out(multiplexer_1_out), .sel(branch_abs));
  nor nor_1 (nor_1_out, branch_rel, branch_abs);
  register register_1 (.reset(reset), .C(C), .D(multiplexer_2_out), .Q(instruction_address));  // open: write
  Multiplexer #(.width(12), .enable("false")) multiplexer_2 (
    .in0(multiplexer_1_out), .in1(n12_bit_cla_1_som), .out(multiplexer_2_out), .sel(nor_1_out));
endmodule

// Register File
module register_file (
  input  [2:0] rt,
  input  [11:0] Data,
  input  write,
  input  [2:0] rs,
  input  clock,
  input  reset,
  input  [2:0] rd,
  output [11:0] R,
  output [11:0] S,
  output [11:0] r0,
  output [11:0] r1,
  output [11:0] r2,
  output [11:0] r3,
  output [11:0] r4,
  output [11:0] r5,
  output [11:0] r6,
  output [11:0] r7
);

  wire AND_2_out, AND_3_out, AND_4_out, AND_5_out, AND_6_out, AND_7_out, AND_out, decoder_1_out1,
       decoder_1_out2, decoder_1_out3, decoder_1_out4, decoder_1_out5, decoder_1_out6, decoder_1_out7;

  and AND (AND_out, write, decoder_1_out1);
  and AND_2 (AND_2_out, write, decoder_1_out2);
  and AND_3 (AND_3_out, write, decoder_1_out3);
  register register_1 (.write(1'b0), .reset(reset), .C(clock), .Q(r0));  // open: D
  register register_2 (.write(AND_out), .reset(reset), .C(clock), .D(Data), .Q(r1));
  register register_3 (.write(AND_2_out), .reset(reset), .C(clock), .D(Data), .Q(r2));
  register register_4 (.write(AND_3_out), .reset(reset), .C(clock), .D(Data), .Q(r3));
  Decoder #(.select(3), .enable("false")) decoder_1 (
    .out1(decoder_1_out1), .out2(decoder_1_out2), .out3(decoder_1_out3), .out4(decoder_1_out4),
    .out5(decoder_1_out5), .out6(decoder_1_out6), .out7(decoder_1_out7), .sel(rd));  // open: out0
  and AND_4 (AND_4_out, write, decoder_1_out4);
  and AND_5 (AND_5_out, write, decoder_1_out5);
  and AND_6 (AND_6_out, write, decoder_1_out6);
  and AND_7 (AND_7_out, write, decoder_1_out7);
  register register_5 (.write(AND_4_out), .reset(reset), .C(clock), .D(Data), .Q(r4));
  register register_6 (.write(AND_5_out), .reset(reset), .C(clock), .D(Data), .Q(r5));
  register register_7 (.write(AND_6_out), .reset(reset), .C(clock), .D(Data), .Q(r6));
  register register_8 (.write(AND_7_out), .reset(reset), .C(clock), .D(Data), .Q(r7));
  Multiplexer #(.select(3), .width(12), .enable("false")) multiplexer_1 (
    .in0(r0), .in1(r1), .in2(r2), .in3(r3), .in4(r4), .in5(r5), .in6(r6), .in7(r7), .out(R), .sel(rt));
  Multiplexer #(.select(3), .width(12), .enable("false")) multiplexer_2 (
    .in0(r0), .in1(r1), .in2(r2), .in3(r3), .in4(r4), .in5(r5), .in6(r6), .in7(r7), .out(S), .sel(rs));
endmodule

module decoder (
  input  [15:0] instruction,
  output [2:0] rt,
  output [3:0] func,
  output [2:0] rs,
  output [2:0] rd,
  output [3:0] op_code,
  output [11:0] imm
);

  wire comparator_1_eq;
  wire [11:0] bit_extender_1_out, bit_extender_2_out;

  assign bit_extender_1_out = {{8{instruction[3]}}, instruction[3:0]};  // Bit_Extender bit_extender_1
  assign bit_extender_2_out = {{4{instruction[7]}}, instruction[7:0]};  // Bit_Extender bit_extender_2
  Comparator #(.width(4)) comparator_1 (.a(instruction[15:12]), .b(4'b1100), .eq(comparator_1_eq));  // open: gt, lt
  Multiplexer #(.width(12), .enable("false")) multiplexer_1 (
    .in0(bit_extender_1_out), .in1(bit_extender_2_out), .out(imm), .sel(comparator_1_eq));

  assign func = instruction[3:0];
  assign op_code = instruction[15:12];
  assign rd = instruction[10:8];
  assign rs = instruction[6:4];
  assign rt = instruction[2:0];

  // Notes on the sheet:
  //   Decoder
endmodule

// Controller
module controller (
  input  [3:0] op_code,
  input  [3:0] func,
  output [3:0] ALU_op,
  output RegWrite,
  output ALUSrc,
  output ALUSrcB,
  output MemRead,
  output MemToReg,
  output MemWrite,
  output ReadRD,
  output BranchRel,
  output BranchAbs
);

  wire decoder_1_out0, decoder_1_out1, decoder_1_out2, decoder_1_out3, decoder_1_out4, decoder_1_out5,
       decoder_1_out6, decoder_1_out7, decoder_1_out8, decoder_1_out9, decoder_1_out13, or_2_out, or_3_out;
  wire [3:0] multiplexer_1_out, multiplexer_2_out;

  Decoder #(.select(4), .enable("false")) decoder_1 (
    .out0(decoder_1_out0), .out1(decoder_1_out1), .out2(decoder_1_out2), .out3(decoder_1_out3),
    .out4(decoder_1_out4), .out5(decoder_1_out5), .out6(decoder_1_out6), .out7(decoder_1_out7),
    .out8(decoder_1_out8), .out9(decoder_1_out9), .out10(MemRead), .out11(MemWrite), .out12(ALUSrc),
    .out13(decoder_1_out13), .sel(op_code));  // open: out14, out15
  // OR_Gate or_1 has open pins: in0=decoder_1_out2, in1=decoder_1_out3, in2=decoder_1_out4, in3=decoder_1_out5, in4=decoder_1_out6, in5=decoder_1_out7, in6=decoder_1_out8, in7=decoder_1_out9, out=open
  or or_2 (or_2_out, MemRead, MemWrite, ALUSrc, decoder_1_out13);
  or or_3 (or_3_out, decoder_1_out0, decoder_1_out1);
  Multiplexer #(.width(4), .enable("false")) multiplexer_1 (
    .in0(4'b0100), .in1(4'b1111), .out(multiplexer_1_out), .sel(ALUSrc));
  Multiplexer #(.width(4), .enable("false")) multiplexer_2 (
    .in0(op_code), .in1(multiplexer_1_out), .out(multiplexer_2_out), .sel(or_2_out));
  Multiplexer #(.width(4), .enable("false")) multiplexer_3 (
    .in0(multiplexer_2_out), .in1(func), .out(ALU_op), .sel(or_3_out));
  not not_1 (RegWrite, MemWrite);
  or or_4 (ALUSrcB, MemRead, MemWrite, decoder_1_out13);

  assign MemToReg = MemRead;
  assign ReadRD = MemWrite;

  // Notes on the sheet:
  //   ALU generate A operation
  //   Controller
  //   ALU add operation
  //   immediate type
  //   Geeft aan de ALU of dat die de volle of geen immediate waarde moet gebruiken
  //   Geeft aan de ALU of dat die wel of geen immediate waarde moet gebruiken voor B
endmodule
