// Logisim project CSA_Project4_Memory.circ as structural Verilog: 7 circuits, main circuit register
module register (
  input  write,
  input  reset,
  input  C,
  input  [11:0] D,
  output [11:0] Q
);

  D_Flip_Flop #(.trigger("falling")) d_ff_1 (
    .clk(C), .D(D[0]), .Q(Q[0]), .en(write), .reset(reset));  // open: Qn, preset
  D_Flip_Flop #(.trigger("falling")) d_ff_2 (
    .clk(C), .D(D[1]), .Q(Q[1]), .en(write), .reset(reset));  // open: Qn, preset
  D_Flip_Flop #(.trigger("falling")) d_ff_3 (
    .clk(C), .D(D[2]), .Q(Q[2]), .en(write), .reset(reset));  // open: Qn, preset
  D_Flip_Flop #(.trigger("falling")) d_ff_4 (
    .clk(C), .D(D[3]), .Q(Q[3]), .en(write), .reset(reset));  // open: Qn, preset
  D_Flip_Flop #(.trigger("falling")) d_ff_5 (
    .clk(C), .D(D[4]), .Q(Q[4]), .en(write), .reset(reset));  // open: Qn, preset
  D_Flip_Flop #(.trigger("falling")) d_ff_6 (
    .clk(C), .D(D[5]), .Q(Q[5]), .en(write), .reset(reset));  // open: Qn, preset
  D_Flip_Flop #(.trigger("falling")) d_ff_7 (
    .clk(C), .D(D[6]), .Q(Q[6]), .en(write), .reset(reset));  // open: Qn, preset
  D_Flip_Flop #(.trigger("falling")) d_ff_8 (
    .clk(C), .D(D[7]), .Q(Q[7]), .en(write), .reset(reset));  // open: Qn, preset
  D_Flip_Flop #(.trigger("falling")) d_ff_9 (
    .clk(C), .D(D[8]), .Q(Q[8]), .en(write), .reset(reset));  // open: Qn, preset
  D_Flip_Flop #(.trigger("falling")) d_ff_10 (
    .clk(C), .D(D[9]), .Q(Q[9]), .en(write), .reset(reset));  // open: Qn, preset
  D_Flip_Flop #(.trigger("falling")) d_ff_11 (
    .clk(C), .D(D[10]), .Q(Q[10]), .en(write), .reset(reset));  // open: Qn, preset
  D_Flip_Flop #(.trigger("falling")) d_ff_12 (
    .clk(C), .D(D[11]), .Q(Q[11]), .en(write), .reset(reset));  // open: Qn, preset

  // Notes on the sheet:
  //   REGISTER
endmodule

module registerfile (
  input  [2:0] rt,
  input  [11:0] Data,
  input  write,
  input  [2:0] rs,
  input  clock,
  input  reset,
  input  [2:0] rd,
  output [11:0] R,
  output [11:0] S
);

  wire AND_2_out, AND_3_out, AND_4_out, AND_5_out, AND_6_out, AND_7_out, AND_out, decoder_1_out1,
       decoder_1_out2, decoder_1_out3, decoder_1_out4, decoder_1_out5, decoder_1_out6, decoder_1_out7;
  wire [11:0] register_1_q, register_2_q, register_3_q, register_4_q, register_5_q, register_6_q,
       register_7_q, register_8_q;

  and AND (AND_out, write, decoder_1_out1);
  and AND_2 (AND_2_out, write, decoder_1_out2);
  and AND_3 (AND_3_out, write, decoder_1_out3);
  register register_1 (.write(1'b0), .reset(reset), .C(clock), .Q(register_1_q));  // open: D
  register register_2 (.write(AND_out), .reset(reset), .C(clock), .D(Data), .Q(register_2_q));
  register register_3 (.write(AND_2_out), .reset(reset), .C(clock), .D(Data), .Q(register_3_q));
  register register_4 (.write(AND_3_out), .reset(reset), .C(clock), .D(Data), .Q(register_4_q));
  Decoder #(.select(3), .enable("false")) decoder_1 (
    .out1(decoder_1_out1), .out2(decoder_1_out2), .out3(decoder_1_out3), .out4(decoder_1_out4),
    .out5(decoder_1_out5), .out6(decoder_1_out6), .out7(decoder_1_out7), .sel(rd));  // open: out0
  and AND_4 (AND_4_out, write, decoder_1_out4);
  and AND_5 (AND_5_out, write, decoder_1_out5);
  and AND_6 (AND_6_out, write, decoder_1_out6);
  and AND_7 (AND_7_out, write, decoder_1_out7);
  register register_5 (.write(AND_4_out), .reset(reset), .C(clock), .D(Data), .Q(register_5_q));
  register register_6 (.write(AND_5_out), .reset(reset), .C(clock), .D(Data), .Q(register_6_q));
  register register_7 (.write(AND_6_out), .reset(reset), .C(clock), .D(Data), .Q(register_7_q));
  register register_8 (.write(AND_7_out), .reset(reset), .C(clock), .D(Data), .Q(register_8_q));
  Multiplexer #(.select(3), .width(12), .enable("false")) multiplexer_1 (
    .in0(register_1_q), .in1(register_2_q), .in2(register_3_q), .in3(register_4_q), .in4(register_5_q),
    .in5(register_6_q), .in6(register_7_q), .in7(register_8_q), .out(R), .sel(rt));
  Multiplexer #(.select(3), .width(12), .enable("false")) multiplexer_2 (
    .in0(register_1_q), .in1(register_2_q), .in2(register_3_q), .in3(register_4_q), .in4(register_5_q),
    .in5(register_6_q), .in6(register_7_q), .in7(register_8_q), .out(S), .sel(rs));

  // Notes on the sheet:
  //   REGISTER FILE
endmodule

module counter (
  input  [11:0] D,
  output [11:0] \output 
);

  wire C_out, comparator_1_eq, comparator_1_gt, or_1_out;
  wire [11:0] bit_extender_1_out, n12_bit_cla_1_som;

  Clock C (.out(C_out));
  _12_Bit_CLA u_12_bit_cla_1 (
    .A(\output ), .B(bit_extender_1_out), .carryIn(1'b0), .Som(n12_bit_cla_1_som));  // open: carryOut, Overflow
  assign bit_extender_1_out = {{11{1'b0}}, 1'b1};  // Bit_Extender bit_extender_1
  register register_1 (.reset(or_1_out), .C(C_out), .D(n12_bit_cla_1_som), .Q(\output ));  // open: write
  or or_1 (or_1_out, comparator_1_gt, comparator_1_eq);
  Comparator #(.width(12)) comparator_1 (.a(\output ), .b(D), .gt(comparator_1_gt), .eq(comparator_1_eq));  // open: lt

  // Notes on the sheet:
  //   input
  //   clock
  //   Functionele Counter
endmodule

module traffic_light (
);

  wire and_1_out, C_out, comparator_1_gt, comparator_2_gt, comparator_3_lt, comparator_4_eq, comparator_4_lt,
       comparator_5_gt, comparator_6_gt, comparator_7_lt, nor_1_out, nor_2_out, or_1_out, or_2_out;
  wire [11:0] bit_extender_1_out, n12_bit_cla_1_som, register_1_q;

  assign bit_extender_1_out = {{11{1'b0}}, 1'b1};  // Bit_Extender bit_extender_1
  Clock C (.out(C_out));
  _12_Bit_CLA u_12_bit_cla_1 (
    .A(register_1_q), .B(bit_extender_1_out), .carryIn(1'b0), .Som(n12_bit_cla_1_som));  // open: carryOut, Overflow
  register register_1 (.reset(comparator_1_gt), .C(C_out), .D(n12_bit_cla_1_som), .Q(register_1_q));  // open: write
  Comparator #(.width(12)) comparator_1 (.a(register_1_q), .b(12'h1c), .gt(comparator_1_gt));  // open: eq, lt
  Comparator #(.width(12)) comparator_2 (.a(12'h8), .b(register_1_q), .gt(comparator_2_gt));  // open: eq, lt
  Comparator #(.width(12)) comparator_3 (.a(12'hc), .b(register_1_q), .lt(comparator_3_lt));  // open: gt, eq
  Comparator #(.width(12)) comparator_4 (
    .a(12'he), .b(register_1_q), .eq(comparator_4_eq), .lt(comparator_4_lt));  // open: gt
  Comparator #(.width(12)) comparator_5 (.a(12'h16), .b(register_1_q), .gt(comparator_5_gt));  // open: eq, lt
  Comparator #(.width(12)) comparator_6 (.a(12'he), .b(register_1_q), .gt(comparator_6_gt));  // open: eq, lt
  Comparator #(.width(12)) comparator_7 (.a(12'h1a), .b(register_1_q), .lt(comparator_7_lt));  // open: gt, eq
  or or_1 (or_1_out, comparator_4_lt, comparator_4_eq);
  and and_1 (and_1_out, or_1_out, comparator_5_gt);
  nor nor_1 (nor_1_out, comparator_2_gt, comparator_3_lt);
  nor nor_2 (nor_2_out, and_1_out, or_2_out);
  or or_2 (or_2_out, comparator_6_gt, comparator_7_lt);
  LED led_1 (.in(comparator_3_lt));
  LED led_2 (.in(nor_1_out));
  LED led_3 (.in(comparator_2_gt));
  LED led_4 (.in(or_2_out));
  LED led_5 (.in(nor_2_out));
  LED led_6 (.in(and_1_out));

  // Notes on the sheet:
  //   clock
  //   Light 1
  //   Light 2
endmodule

module stack (
  input  Push,
  input  Pop,
  input  [11:0] Data,
  input  C,
  input  reset,
  output [11:0] Data_2,
  output error
);

  wire count_on_demand_1_out_6, nor_1_out, not_1_out;
  wire [11:0] controlled_buffer_1_out, count_on_demand_1_output;

  nor nor_1 (nor_1_out, Pop, Push);
  not not_1 (not_1_out, C);
  count_on_demand count_on_demand_1 (
    .add_1(Push), .sub_1(Pop), .reset(reset), .clock(C), .\output (count_on_demand_1_output),
    .out_6(count_on_demand_1_out_6));
  assign controlled_buffer_1_out = Push ? Data : 12'bz;  // Controlled_Buffer controlled_buffer_1
  assign controlled_buffer_1_out = Pop ? {12{1'b0}} : 12'bz;  // Controlled_Buffer controlled_buffer_2
  RAM #(.addrWidth(12), .dataWidth(12)) ram_1 (
    .addr(count_on_demand_1_output), .data(controlled_buffer_1_out), .clk(not_1_out), .ld(nor_1_out),
    .clr(reset));  // open: sel
  Multiplexer #(.width(12)) multiplexer_1 (
    .in0({12{1'b0}}), .in1(controlled_buffer_1_out), .out(Data_2), .sel(nor_1_out));  // open: en
  buf or_1 (error, count_on_demand_1_out_6);  // OR_Gate
endmodule

module count_on_demand (
  input  add_1,
  input  sub_1,
  input  reset,
  input  clock,
  output [11:0] \output ,
  output out_6
);

  wire and_1_out, and_3_out, is_null_1_is_nil, is_null_2_is_nil, is_null_3_is_nil, or_2_out;
  wire [11:0] and_2_out, bit_extender_1_out, bit_extender_2_out, bit_extender_3_out, multiplexer_1_out,
       n12_bit_cla_1_som, n12_bit_cla_2_som, not_1_out, not_2_out, or_1_out, register_1_q, xor_1_out;

  and and_1 (and_1_out, add_1, sub_1);
  assign bit_extender_1_out = {{11{1'b0}}, add_1};  // Bit_Extender bit_extender_1
  assign bit_extender_2_out = {{11{sub_1}}, sub_1};  // Bit_Extender bit_extender_2
  assign bit_extender_3_out = {{11{and_1_out}}, and_1_out};  // Bit_Extender bit_extender_3
  assign or_1_out = bit_extender_1_out | bit_extender_2_out;  // OR_Gate or_1, 12 bits wide
  _12_Bit_CLA u_12_bit_cla_1 (
    .A(register_1_q), .B(xor_1_out), .carryIn(1'b0), .Som(n12_bit_cla_1_som));  // open: carryOut, Overflow
  assign xor_1_out = or_1_out ^ bit_extender_3_out;  // XOR_Gate xor_1, 12 bits wide
  register register_1 (.reset(or_2_out), .C(clock), .D(n12_bit_cla_1_som), .Q(register_1_q));  // open: write
  or or_2 (or_2_out, reset, and_3_out);
  assign not_1_out = ~register_1_q;  // NOT_Gate not_1, 12 bits wide
  assign not_2_out = ~bit_extender_2_out;  // NOT_Gate not_2, 12 bits wide
  is_null is_null_1 (.in_1(register_1_q), .is_nil(is_null_1_is_nil));
  is_null is_null_2 (.in_1(register_1_q), .is_nil(is_null_2_is_nil));
  assign and_2_out = not_1_out & not_2_out;  // AND_Gate and_2, 12 bits wide
  and and_3 (and_3_out, is_null_1_is_nil, sub_1);
  _12_Bit_CLA u_12_bit_cla_2 (
    .A(register_1_q), .B({12{1'b1}}), .carryIn(1'b0), .Som(n12_bit_cla_2_som));  // open: carryOut, Overflow
  is_null is_null_3 (.in_1(and_2_out), .is_nil(is_null_3_is_nil));
  Multiplexer #(.width(12)) multiplexer_1 (
    .in0(n12_bit_cla_2_som), .in1(register_1_q), .out(multiplexer_1_out), .sel(add_1));  // open: en
  Multiplexer #(.width(12)) multiplexer_2 (
    .in0(multiplexer_1_out), .in1({12{1'b0}}), .out(\output ), .sel(is_null_2_is_nil));  // open: en
  or or_3 (out_6, and_1_out, is_null_3_is_nil);
endmodule

module is_null (
  input  [11:0] in_1,
  output is_nil
);

  wire [11:0] not_1_out;

  assign not_1_out = ~in_1;  // NOT_Gate not_1, 12 bits wide
  and and_1 (is_nil, not_1_out[0], not_1_out[1], not_1_out[2], not_1_out[3], not_1_out[4], not_1_out[5], not_1_out[7], not_1_out[8], not_1_out[9], not_1_out[10], not_1_out[11]);
endmodule
