// Logisim project SD_Group05.circ as structural Verilog: 6 circuits, main circuit main
module main (
  output [11:0] pc,
  output [11:0] r0,
  output [11:0] r1,
  output [11:0] r2,
  output [11:0] r3,
  output [11:0] r4,
  output [11:0] r5,
  output [11:0] r6,
  output [11:0] r7,
  output halt
);

  wire and_1_out, and_2_out, bitselector_1_out, clock_1_out, controller_1_alusrc, controller_1_alusrcb,
       controller_1_branchabs, controller_1_branchrel, controller_1_linkaddress, controller_1_memread,
       controller_1_memtoreg, controller_1_memwrite, controller_1_readrd, controller_1_regwrite,
       controller_1_usetargetaddress, reset_out;
  wire [2:0] decoder_1_rd, decoder_1_rs, decoder_1_rt, multiplexer_4_out, multiplexer_5_out;
  wire [3:0] controller_1_alu_op, decoder_1_func, decoder_1_op_code;
  wire [11:0] bit_extender_1_out, decoder_1_imm, decoder_1_target_address, multiplexer_1_out,
       multiplexer_2_out, multiplexer_3_out, multiplexer_6_out, multiplexer_7_out, multiplexer_8_out,
       multiplexer_9_out, multiplexer_10_out, n12_bit_alu_1_result, n12_bit_cla_1_som, ram_2_data,
       register_file_1_r, register_file_1_s;
  wire [15:0] ram_1_data;

  Halt halt_1 (.instruction(ram_1_data), .clock(clock_1_out), .reset(reset_out), .halt(halt));
  Clock clock_1 (.out(clock_1_out));
  Button reset (.out(reset_out));
  BitSelector #(.width(12)) bitselector_1 (.in(n12_bit_alu_1_result), .out(bitselector_1_out), .sel(4'b0000));
  Multiplexer #(.width(12), .enable("false")) multiplexer_1 (
    .in0(multiplexer_2_out), .in1(decoder_1_imm), .out(multiplexer_1_out), .sel(and_2_out));
  Multiplexer #(.width(12), .enable("false")) multiplexer_2 (
    .in0(n12_bit_alu_1_result), .in1(decoder_1_target_address), .out(multiplexer_2_out),
    .sel(controller_1_usetargetaddress));
  and and_1 (and_1_out, ~halt, clock_1_out);  // AND_Gate
  and and_2 (and_2_out, bitselector_1_out, controller_1_branchrel);
  PC pc_1 (
    .branch_rel(and_2_out), .branch_abs(controller_1_branchabs), .branch_val(multiplexer_1_out),
    .C(and_1_out), .reset(reset_out), .instruction_address(pc));
  assign bit_extender_1_out = {{11{1'b0}}, 1'b1};  // Bit_Extender bit_extender_1
  decoder decoder_1 (
    .instruction(ram_1_data), .rt(decoder_1_rt), .func(decoder_1_func), .rs(decoder_1_rs), .rd(decoder_1_rd),
    .op_code(decoder_1_op_code), .imm(decoder_1_imm), .target_address(decoder_1_target_address));
  _12_Bit_CLA u_12_bit_cla_1 (
    .A(pc), .B(bit_extender_1_out), .carryIn(1'b0), .Som(n12_bit_cla_1_som));  // open: carryOut, Overflow
  RAM #(.addrWidth(12), .dataWidth(16)) ram_1 (
    .addr(pc), .data(ram_1_data), .clk(and_1_out), .ld(1'b1));  // open: sel, clr
  Multiplexer #(.width(12), .enable("false")) multiplexer_3 (
    .in0(multiplexer_10_out), .in1(n12_bit_cla_1_som), .out(multiplexer_3_out), .sel(controller_1_linkaddress));
  controller controller_1 (
    .op_code(decoder_1_op_code), .func(decoder_1_func), .ALU_op(controller_1_alu_op),
    .RegWrite(controller_1_regwrite), .ALUSrc(controller_1_alusrc), .ALUSrcB(controller_1_alusrcb),
    .MemRead(controller_1_memread), .MemToReg(controller_1_memtoreg), .MemWrite(controller_1_memwrite),
    .BranchRel(controller_1_branchrel), .BranchAbs(controller_1_branchabs), .ReadRD(controller_1_readrd),
    .LinkAddress(controller_1_linkaddress), .UseTargetAddress(controller_1_usetargetaddress));
  Multiplexer #(.width(3), .enable("false")) multiplexer_4 (
    .in0(decoder_1_rt), .in1(decoder_1_rd), .out(multiplexer_4_out), .sel(controller_1_readrd));
  Multiplexer #(.width(3), .enable("false")) multiplexer_5 (
    .in0(decoder_1_rd), .in1(3'b111), .out(multiplexer_5_out), .sel(controller_1_linkaddress));
  register_file register_file_1 (
    .Data(multiplexer_3_out), .write(controller_1_regwrite), .R(register_file_1_r), .S(register_file_1_s),
    .r1(r1), .r2(r2), .r3(r3), .r4(r4), .rd(multiplexer_5_out), .r5(r5), .r6(r6), .r7(r7),
    .rt(multiplexer_4_out), .rs(decoder_1_rs), .clock(and_1_out), .reset(reset_out), .r0(r0));
  Multiplexer #(.width(12), .enable("false")) multiplexer_6 (
    .in0(register_file_1_s), .in1(decoder_1_imm), .out(multiplexer_6_out), .sel(controller_1_alusrc));
  Multiplexer #(.width(12), .enable("false")) multiplexer_7 (
    .in0(register_file_1_r), .in1(decoder_1_imm), .out(multiplexer_7_out), .sel(controller_1_alusrcb));
  Multiplexer #(.width(12), .enable("false")) multiplexer_8 (
    .in0(multiplexer_6_out), .in1(multiplexer_7_out), .out(multiplexer_8_out), .sel(controller_1_branchrel));
  _12_bit_ALU u_12_bit_alu_1 (
    .ALU_code(controller_1_alu_op), .a(multiplexer_8_out), .b(multiplexer_9_out),
    .result(n12_bit_alu_1_result));  // open: overflow
  Multiplexer #(.width(12), .enable("false")) multiplexer_9 (
    .in0(multiplexer_7_out), .in1(multiplexer_6_out), .out(multiplexer_9_out), .sel(controller_1_branchrel));
  Multiplexer #(.width(12), .enable("false")) multiplexer_10 (
    .in0(n12_bit_alu_1_result), .in1(ram_2_data), .out(multiplexer_10_out), .sel(controller_1_memtoreg));
  RAM #(.addrWidth(12), .dataWidth(12), .bus("separate")) ram_2 (
    .addr(n12_bit_alu_1_result), .din(register_file_1_r), .data(ram_2_data), .str(controller_1_memwrite),
    .clk(and_1_out), .ld(controller_1_memread), .clr(reset_out));  // open: sel

  // Notes on the sheet:
  //   current instruction
  //   clock signal
  //   reset button
  //   DO NOT CHANGE THE INPUTS AND OUTPUTS OF THIS CIRCUIT! Do not add/remove inputs or outputs. Do not even change their location or orientation.
endmodule

module Halt (
  input  [15:0] instruction,
  input  clock,
  input  reset,
  output halt
);

  wire and_1_out, comparator_1_eq, comparator_2_gt, counter_1_carry, or_1_out, or_2_out;
  wire [11:0] counter_1_q;

  Comparator #(.width(16), .mode("unsigned")) comparator_1 (
    .a(instruction), .b({16{1'b0}}), .eq(comparator_1_eq));  // open: gt, lt
  Counter #(.width(12), .max('hfff), .trigger("falling")) counter_1 (
    .Q(counter_1_q), .carry(counter_1_carry), .clk(clock), .clr(reset));  // open: load, D, count
  or or_1 (or_1_out, comparator_1_eq, counter_1_carry);
  Comparator #(.width(12), .mode("unsigned")) comparator_2 (
    .a(counter_1_q), .b({12{1'b0}}), .gt(comparator_2_gt));  // open: eq, lt
  or or_2 (or_2_out, halt, and_1_out);
  and and_1 (and_1_out, or_1_out, comparator_2_gt);
  Register #(.width(1)) register_1 (.D(or_2_out), .Q(halt), .clk(clock), .clr(reset));  // open: en

  // Notes on the sheet:
  //   halt becomes and stays asserted if the instruction is 0000 (not in the first clock cycle) or the end of the counter is reached (2^12)
endmodule

module PC (
  input  branch_rel,
  input  branch_abs,
  input  [11:0] branch_val,
  input  C,
  input  reset,
  output [11:0] instruction_address
);

  wire nor_1_out;
  wire [11:0] bit_extender_1_out, multiplexer_1_out, multiplexer_2_out, n12_bit_cla_1_som, n12_bit_cla_2_som;

  assign bit_extender_1_out = {{11{1'b0}}, 1'b1};  // Bit_Extender bit_extender_1
  _12_Bit_CLA u_12_bit_cla_1 (
    .A(bit_extender_1_out), .B(instruction_address), .carryIn(1'b0), .Som(n12_bit_cla_1_som));  // open: carryOut, Overflow
  _12_Bit_CLA u_12_bit_cla_2 (
    .A(branch_val), .B(instruction_address), .carryIn(1'b1), .Som(n12_bit_cla_2_som));  // open: carryOut, Overflow
  Multiplexer #(.width(12), .enable("false")) multiplexer_1 (
    .in0(n12_bit_cla_2_som), .in1(branch_val), .out(multiplexer_1_out), .sel(branch_abs));
  nor nor_1 (nor_1_out, branch_rel, branch_abs);
  Multiplexer #(.width(12), .enable("false")) multiplexer_2 (
    .in0(multiplexer_1_out), .in1(n12_bit_cla_1_som), .out(multiplexer_2_out), .sel(nor_1_out));
  register register_1 (.reset(reset), .C(C), .D(multiplexer_2_out), .Q(instruction_address));  // open: write
endmodule

// Register File
module register_file (
  input  [2:0] rt,
  input  [11:0] Data,
  input  write,
  input  [2:0] rs,
  input  clock,
  input  reset,
  input  [2:0] rd,
  output [11:0] R,
  output [11:0] S,
  output [11:0] r0,
  output [11:0] r1,
  output [11:0] r2,
  output [11:0] r3,
  output [11:0] r4,
  output [11:0] r5,
  output [11:0] r6,
  output [11:0] r7
);

  wire AND_2_out, AND_3_out, AND_4_out, AND_5_out, AND_6_out, AND_7_out, AND_out, decoder_1_out1,
       decoder_1_out2, decoder_1_out3, decoder_1_out4, decoder_1_out5, decoder_1_out6, decoder_1_out7;

  and AND (AND_out, write, decoder_1_out1);
  and AND_2 (AND_2_out, write, decoder_1_out2);
  and AND_3 (AND_3_out, write, decoder_1_out3);
  register register_1 (.write(1'b0), .reset(reset), .C(clock), .Q(r0));  // open: D
  register register_2 (.write(AND_out), .reset(reset), .C(clock), .D(Data), .Q(r1));
  register register_3 (.write(AND_2_out), .reset(reset), .C(clock), .D(Data), .Q(r2));
  register register_4 (.write(AND_3_out), .reset(reset), .C(clock), .D(Data), .Q(r3));
  Decoder #(.select(3), .enable("false")) decoder_1 (
    .out1(decoder_1_out1), .out2(decoder_1_out2), .out3(decoder_1_out3), .out4(decoder_1_out4),
    .out5(decoder_1_out5), .out6(decoder_1_out6), .out7(decoder_1_out7), .sel(rd));  // open: out0
  and AND_4 (AND_4_out, write, decoder_1_out4);
  and AND_5 (AND_5_out, write, decoder_1_out5);
  and AND_6 (AND_6_out, write, decoder_1_out6);
  and AND_7 (AND_7_out, write, decoder_1_out7);
  register register_5 (.write(AND_4_out), .reset(reset), .C(clock), .D(Data), .Q(r4));
  register register_6 (.write(AND_5_out), .reset(reset), .C(clock), .D(Data), .Q(r5));
  register register_7 (.write(AND_6_out), .reset(reset), .C(clock), .D(Data), .Q(r6));
  register register_8 (.write(AND_7_out), .reset(reset), .C(clock), .D(Data), .Q(r7));
  Multiplexer #(.select(3), .width(12), .enable("false")) multiplexer_1 (
    .in0(r0), .in1(r1), .in2(r2), .in3(r3), .in4(r4), .in5(r5), .in6(r6), .in7(r7), .out(R), .sel(rt));
  Multiplexer #(.select(3), .width(12), .enable("false")) multiplexer_2 (
    .in0(r0), .in1(r1), .in2(r2), .in3(r3), .in4(r4), .in5(r5), .in6(r6), .in7(r7), .out(S), .sel(rs));
endmodule

module decoder (
  input  [15:0] instruction,
  output [2:0] rt,
  output [3:0] func,
  output [2:0] rs,
  output [2:0] rd,
  output [3:0] op_code,
  output [11:0] imm,
  output [11:0] target_address
);

  wire comparator_1_eq, comparator_2_eq, comparator_3_eq, comparator_4_eq, comparator_5_eq, nand_1_out,
       nor_1_out;
  wire [11:0] bit_extender_1_out, bit_extender_2_out, bit_extender_3_out, bit_extender_4_out,
       multiplexer_1_out, multiplexer_3_out;

  assign bit_extender_1_out = {{8{instruction[7]}}, instruction[7:4]};  // Bit_Extender bit_extender_1
  assign bit_extender_2_out = {{8{1'b0}}, instruction[3:0]};  // Bit_Extender bit_extender_2
  assign bit_extender_3_out = {{8{instruction[3]}}, instruction[3:0]};  // Bit_Extender bit_extender_3
  assign bit_extender_4_out = {{4{instruction[7]}}, instruction[7:0]};  // Bit_Extender bit_extender_4
  Comparator #(.width(4), .mode("unsigned")) comparator_1 (
    .a(instruction[15:12]), .b(4'b0001), .eq(comparator_1_eq));  // open: gt, lt
  Comparator #(.width(4), .mode("unsigned")) comparator_2 (
    .a(instruction[3:0]), .b(4'b0010), .eq(comparator_2_eq));  // open: gt, lt
  Comparator #(.width(4), .mode("unsigned")) comparator_3 (
    .a(instruction[15:12]), .b(4'b1010), .eq(comparator_3_eq));  // open: gt, lt
  Comparator #(.width(4)) comparator_4 (.a(instruction[15:12]), .b(4'b1011), .eq(comparator_4_eq));  // open: gt, lt
  Comparator #(.width(4)) comparator_5 (.a(instruction[15:12]), .b(4'b1100), .eq(comparator_5_eq));  // open: gt, lt
  assign target_address = {{4{instruction[11]}}, instruction[11:4]};  // Bit_Extender bit_extender_5
  nor nor_1 (nor_1_out, comparator_4_eq, comparator_3_eq);
  Multiplexer #(.width(12), .enable("false")) multiplexer_1 (
    .in0(bit_extender_2_out), .in1(bit_extender_3_out), .out(multiplexer_1_out), .sel(nor_1_out));
  nand nand_1 (nand_1_out, comparator_1_eq, comparator_2_eq);
  Multiplexer #(.width(12), .enable("false")) multiplexer_2 (
    .in0(bit_extender_1_out), .in1(multiplexer_3_out), .out(imm), .sel(nand_1_out));
  Multiplexer #(.width(12), .enable("false")) multiplexer_3 (
    .in0(multiplexer_1_out), .in1(bit_extender_4_out), .out(multiplexer_3_out), .sel(comparator_5_eq));

  assign func = instruction[3:0];
  assign op_code = instruction[15:12];
  assign rd = instruction[10:8];
  assign rs = instruction[6:4];
  assign rt = instruction[2:0];

  // Notes on the sheet:
  //   Decoder
endmodule

// Controller
module controller (
  input  [3:0] op_code,
  input  [3:0] func,
  output [3:0] ALU_op,
  output RegWrite,
  output ALUSrc,
  output ALUSrcB,
  output MemRead,
  output MemToReg,
  output MemWrite,
  output ReadRD,
  output BranchRel,
  output BranchAbs,
  output LinkAddress,
  output UseTargetAddress
);

  wire and_1_out, and_2_out, and_3_out, and_4_out, decoder_1_out2, decoder_1_out3, decoder_1_out4,
       decoder_2_out0, decoder_2_out1, decoder_2_out12, decoder_2_out13, decoder_2_out14, decoder_2_out15,
       or_1_out, or_2_out, or_3_out, or_4_out, or_8_out;
  wire [3:0] multiplexer_1_out, multiplexer_2_out, multiplexer_3_out, multiplexer_4_out, multiplexer_6_out;

  Decoder #(.select(4), .enable("false")) decoder_1 (
    .out2(decoder_1_out2), .out3(decoder_1_out3), .out4(decoder_1_out4), .sel(func));  // open: out0, out1, out5, out6, out7, out8, out9, out10, out11, out12, out13, out14, out15
  Decoder #(.select(4), .enable("false")) decoder_2 (
    .out0(decoder_2_out0), .out1(decoder_2_out1), .out10(MemRead), .out11(MemWrite), .out12(decoder_2_out12),
    .out13(decoder_2_out13), .out14(decoder_2_out14), .out15(decoder_2_out15), .sel(op_code));  // open: out2, out3, out4, out5, out6, out7, out8, out9
  Multiplexer #(.width(4), .enable("false")) multiplexer_1 (
    .in0(4'b1000), .in1(4'b0110), .out(multiplexer_1_out), .sel(decoder_2_out15));
  or or_1 (or_1_out, MemRead, MemWrite, decoder_2_out12, decoder_2_out13);
  or or_2 (or_2_out, decoder_2_out0, decoder_2_out1);
  Multiplexer #(.width(4), .enable("false")) multiplexer_2 (
    .in0(4'b0100), .in1(4'b1111), .out(multiplexer_2_out), .sel(decoder_2_out12));
  Multiplexer #(.width(4), .enable("false")) multiplexer_3 (
    .in0(op_code), .in1(multiplexer_2_out), .out(multiplexer_3_out), .sel(or_1_out));
  Multiplexer #(.width(4), .enable("false")) multiplexer_4 (
    .in0(multiplexer_3_out), .in1(multiplexer_1_out), .out(multiplexer_4_out), .sel(or_3_out));
  or or_3 (or_3_out, decoder_2_out14, decoder_2_out15);
  Multiplexer #(.width(4), .enable("false")) multiplexer_5 (
    .in0(multiplexer_4_out), .in1(multiplexer_6_out), .out(ALU_op), .sel(or_2_out));
  Multiplexer #(.width(4), .enable("false")) multiplexer_6 (
    .in0(func), .in1(4'b0100), .out(multiplexer_6_out), .sel(decoder_1_out2));
  and and_1 (and_1_out, decoder_1_out3, decoder_2_out1);
  and and_2 (and_2_out, decoder_1_out2, decoder_2_out1);
  or or_4 (or_4_out, decoder_1_out2, decoder_1_out3, decoder_1_out4);
  nor nor_1 (RegWrite, and_1_out, MemWrite, and_3_out, decoder_2_out14, decoder_2_out15);
  and and_3 (and_3_out, decoder_2_out1, decoder_1_out2);
  and and_4 (and_4_out, decoder_2_out1, decoder_1_out2);
  or or_5 (ALUSrcB, MemRead, MemWrite, decoder_2_out13);
  or or_6 (ReadRD, MemWrite, decoder_2_out14, decoder_2_out15, and_2_out);
  or or_7 (BranchRel, decoder_2_out14, decoder_2_out15);
  and and_5 (BranchAbs, decoder_2_out1, or_4_out);
  and and_6 (LinkAddress, decoder_2_out1, decoder_1_out4);
  and and_7 (UseTargetAddress, decoder_2_out1, or_8_out);
  or or_8 (or_8_out, decoder_1_out4, decoder_1_out3);
  or or_9 (ALUSrc, decoder_2_out12, and_4_out);

  assign MemToReg = MemRead;

  // Notes on the sheet:
  //   ALU generate A operation
  //   Controller
  //   ALU eq operation
  //   ALU lt operation
  //   ALU add operation
  //   immediate type
  //   Geeft aan de ALU of dat die de volle of geen immediate waarde moet gebruiken
  //   Geeft aan de ALU of dat die wel of geen immediate waarde moet gebruiken voor B
endmodule
